// Logisim project 8 bit ALU.circ as structural Verilog: 1 circuit, main circuit ALU
module ALU (
  input  [7:0] Flag_in_cff6aa82,
  input  [7:0] A,
  input  [7:0] B,
  input  [3:0] OpCode,
  output [7:0] Flag_Out_e4e05d57,
  output [7:0] Result
);

  wire and_2_out, Cout, l_4_16_decoder_8be9e253_1_l_8_d487730e, l_4_16_decoder_8be9e253_1_l_9_cbca2fb9,
       l_4_16_decoder_8be9e253_1_l_10_a4afafe6, l_4_16_decoder_8be9e253_1_l_11_b30431ab, mux_1_2_y, or_2_out,
       xnor_1_0184103f_1_y, xor_1_e881abe8_1_y, xor_1_e881abe8_2_y, xor_1_e881abe8_3_y;
  wire [1:0] nor_2_out;
  wire [6:0] full_adder_8_b59b4ad2_1_sum;
  wire [7:0] and_1_out, Bout, l_1_8_bit_extender_8f3d069e_1_y, left_shifter_336d19af_1_out_2, not_1_out,
       or_1_out, right_shifter_531e43bc_1_out_2, xor_8_4b3caf6e_1_y;

  Xor_8_4b3caf6e xor_8_4b3caf6e_1 (.A(B), .B(A), .Y(xor_8_4b3caf6e_1_y));
  L_1_8_Bit_extender_8f3d069e l_1_8_bit_extender_8f3d069e_1 (
    .A(Flag_Out_e4e05d57[7]), .Y(l_1_8_bit_extender_8f3d069e_1_y));
  assign or_1_out = A | B;  // OR_Gate or_1, 8 bits wide
  Left_Shifter_336d19af left_shifter_336d19af_1 (.in_1(A), .out_2(left_shifter_336d19af_1_out_2));
  Right_Shifter_531e43bc right_shifter_531e43bc_1 (.in_1(A), .out_2(right_shifter_531e43bc_1_out_2));
  Mux_8 mux_8_1 (
    .p4(or_1_out), .p5(xor_8_4b3caf6e_1_y), .p6(left_shifter_336d19af_1_out_2),
    .p7(right_shifter_531e43bc_1_out_2), .p8({A[6:0], Flag_in_cff6aa82[0]}),
    .p9({Flag_in_cff6aa82[0], A[7:1]}), .p10({Flag_Out_e4e05d57[7], full_adder_8_b59b4ad2_1_sum}),
    .p11({Flag_Out_e4e05d57[7], full_adder_8_b59b4ad2_1_sum}),
    .p0({Flag_Out_e4e05d57[7], full_adder_8_b59b4ad2_1_sum}),
    .p1({Flag_Out_e4e05d57[7], full_adder_8_b59b4ad2_1_sum}), .p2(and_1_out),
    .p3(l_1_8_bit_extender_8f3d069e_1_y), .in_16(OpCode), .out_18(Result));  // open: p12, p13, p14, p15
  assign not_1_out = ~B;  // NOT_Gate not_1, 8 bits wide
  Mux_8 mux_8_2 (.p0(B), .p1(not_1_out), .Select(OpCode[0]), .Y(Bout));
  Full_Adder_8_b59b4ad2 full_adder_8_b59b4ad2_1 (
    .in_2(Bout), .in_3(A), .Cin(OpCode[0]), .Sum({Flag_Out_e4e05d57[7], full_adder_8_b59b4ad2_1_sum}),
    .Cout(Cout));
  assign and_1_out = A & B;  // AND_Gate and_1, 8 bits wide
  Xor_1_e881abe8 xor_1_e881abe8_1 (.A(B[4]), .B(A[3]), .Y(xor_1_e881abe8_1_y));
  Mux_1 mux_1_1 (
    .p0(xor_1_e881abe8_1_y), .p1(xor_1_e881abe8_2_y), .Select(full_adder_8_b59b4ad2_1_sum[5]),
    .Y(Flag_Out_e4e05d57[4]));
  Xor_1_e881abe8 xor_1_e881abe8_2 (.A(A[3]), .B(B[3]), .Y(xor_1_e881abe8_2_y));
  L_8_1_Parity_cb529c41 l_8_1_parity_cb529c41_1 (
    .C(Result[2]), .D(Result[3]), .E(Result[4]), .F(Result[5]), .G(Result[6]), .H(Result[7]), .A(Result[0]),
    .B(Result[1]), .Y(Flag_Out_e4e05d57[2]));
  Mux_1 mux_1_2 (.p0(A[7]), .p1(A[0]), .Select(OpCode[0]), .Y(mux_1_2_y));
  nor nor_1 (Flag_Out_e4e05d57[6], Result[0], Result[1], Result[2], Result[3], Result[4], Result[5], Result[6], Result[7]);
  L_4_16_Decoder_8be9e253 l_4_16_decoder_8be9e253_1 (
    .Select(OpCode), .En(1'b1), .L_8_d487730e(l_4_16_decoder_8be9e253_1_l_8_d487730e),
    .L_9_cbca2fb9(l_4_16_decoder_8be9e253_1_l_9_cbca2fb9),
    .L_10_a4afafe6(l_4_16_decoder_8be9e253_1_l_10_a4afafe6),
    .L_11_b30431ab(l_4_16_decoder_8be9e253_1_l_11_b30431ab));  // open: L_1_2e59f046, L_2_6856bdbb, L_3_5fdef051, L_4_9228b5c5, L_5_b57ff108, L_6_230831cd, L_7_3664e176, L_12_6f7bd373, L_13_da15d73d, L_14_ce2deec9, L_15_abfab048, L_0_71f7447a
  XNor_1_0184103f xnor_1_0184103f_1 (.A(A[7]), .B(Bout[7]), .Y(xnor_1_0184103f_1_y));
  Xor_1_e881abe8 xor_1_e881abe8_3 (.A(Bout[7]), .B(Flag_Out_e4e05d57[7]), .Y(xor_1_e881abe8_3_y));
  or or_2 (or_2_out, l_4_16_decoder_8be9e253_1_l_8_d487730e, l_4_16_decoder_8be9e253_1_l_9_cbca2fb9);
  and and_2 (and_2_out, xnor_1_0184103f_1_y, OpCode[3], xor_1_e881abe8_3_y);
  Mux_1 mux_1_3 (
    .Select(nor_2_out), .p2(Flag_in_cff6aa82[0]), .p3(Cout), .p0(mux_1_2_y), .p1(and_2_out),
    .Y(Flag_Out_e4e05d57[0]));
  or or_3 (nor_2_out[1], l_4_16_decoder_8be9e253_1_l_11_b30431ab, l_4_16_decoder_8be9e253_1_l_10_a4afafe6);
  nor nor_2 (nor_2_out[0], l_4_16_decoder_8be9e253_1_l_10_a4afafe6, or_2_out);

  assign {Flag_Out_e4e05d57[5], Flag_Out_e4e05d57[3], Flag_Out_e4e05d57[1]} = 3'b001;

  // Other names for the same wires on the sheet: Fin[7:0] = Flag_in_cff6aa82; S = Flag_Out_e4e05d57[7];
  //   CY = Flag_Out_e4e05d57[0]; P = Flag_Out_e4e05d57[2]; AC = Flag_Out_e4e05d57[4]; Z = Flag_Out_e4e05d57[6];
  //   OP[3:0] = OpCode

  // Notes on the sheet:
  //   Fin 0 is Carry
  //   ALU Codes:
  //   0 Add
  //   1 Subtract
  //   2 A and B
  //   3 A < B
  //   4 A or B
  //   5 A Xor B
  //   6 Shift A left
  //   7 Shift A right
  //   10 Add with carry
  //   11 Subtract with borrow
  //   8 Shift A left through carry
  //   9 Shift A right through carry
endmodule
