// Logisim project Equals.circ as structural Verilog: 2 circuits, main circuit Equals_1_4de0c3f0
module Equals_1_4de0c3f0 (
  input  A,
  input  B,
  output Y
);

  wire and_1_out, and_2_out, nor_1_out;

  and and_1 (and_1_out, A, ~B);  // AND_Gate
  and and_2 (and_2_out, ~A, B);  // AND_Gate
  nor nor_1 (nor_1_out, and_1_out, and_2_out);
  Error_to_high_1_d72b71e8 error_to_high_1_d72b71e8_1 (.In(nor_1_out), .Out(Y));
endmodule

module Equals_8_f6a9e01b (
  input  [7:0] A,
  input  [7:0] B,
  output Y
);

  wire [7:0] and_1_out, and_2_out, error_to_high_8_255a56c3_1_out, nor_1_out;

  assign and_1_out = A & ~B;  // AND_Gate and_1, 8 bits wide
  assign and_2_out = ~A & B;  // AND_Gate and_2, 8 bits wide
  assign nor_1_out = ~(and_1_out | and_2_out);  // NOR_Gate nor_1, 8 bits wide
  and and_3 (Y, error_to_high_8_255a56c3_1_out[0], error_to_high_8_255a56c3_1_out[1], error_to_high_8_255a56c3_1_out[2], error_to_high_8_255a56c3_1_out[3], error_to_high_8_255a56c3_1_out[4], error_to_high_8_255a56c3_1_out[5], error_to_high_8_255a56c3_1_out[6], error_to_high_8_255a56c3_1_out[7]);
  Error_to_high_8_255a56c3 error_to_high_8_255a56c3_1 (.In(nor_1_out), .Out(error_to_high_8_255a56c3_1_out));
endmodule
