// Logisim project Incrementer and decrementer.circ as structural Verilog: 5 circuits, main circuit Inc_dec_16_1df549c4
module Inc_dec_16_1df549c4 (
  input  [15:0] In,
  input  Inc_Dec_32c9cf86,
  input  Carry_Barrow_In_ee85c3ba,
  output Carry_Barrow_Out_8faccd5f,
  output [15:0] Out
);

  wire inc_dec_2_22b879e6_2_carry_barrow_out_8faccd5f, inc_dec_2_22b879e6_3_carry_barrow_out_8faccd5f,
       inc_dec_2_22b879e6_4_carry_barrow_out_8faccd5f, inc_dec_2_22b879e6_5_carry_barrow_out_8faccd5f,
       inc_dec_2_22b879e6_6_carry_barrow_out_8faccd5f, inc_dec_2_22b879e6_7_carry_barrow_out_8faccd5f,
       inc_dec_2_22b879e6_8_carry_barrow_out_8faccd5f;

  Inc_dec_2_22b879e6 inc_dec_2_22b879e6_1 (
    .Inc_Dec_32c9cf86(Inc_Dec_32c9cf86), .In(In[15:14]),
    .Carry_Barrow_In_ee85c3ba(inc_dec_2_22b879e6_2_carry_barrow_out_8faccd5f), .Out(Out[15:14]),
    .Carry_Barrow_Out_8faccd5f(Carry_Barrow_Out_8faccd5f));
  Inc_dec_2_22b879e6 inc_dec_2_22b879e6_2 (
    .Inc_Dec_32c9cf86(Inc_Dec_32c9cf86), .In(In[13:12]),
    .Carry_Barrow_In_ee85c3ba(inc_dec_2_22b879e6_3_carry_barrow_out_8faccd5f), .Out(Out[13:12]),
    .Carry_Barrow_Out_8faccd5f(inc_dec_2_22b879e6_2_carry_barrow_out_8faccd5f));
  Inc_dec_2_22b879e6 inc_dec_2_22b879e6_3 (
    .Inc_Dec_32c9cf86(Inc_Dec_32c9cf86), .In(In[11:10]),
    .Carry_Barrow_In_ee85c3ba(inc_dec_2_22b879e6_4_carry_barrow_out_8faccd5f), .Out(Out[11:10]),
    .Carry_Barrow_Out_8faccd5f(inc_dec_2_22b879e6_3_carry_barrow_out_8faccd5f));
  Inc_dec_2_22b879e6 inc_dec_2_22b879e6_4 (
    .Inc_Dec_32c9cf86(Inc_Dec_32c9cf86), .In(In[9:8]),
    .Carry_Barrow_In_ee85c3ba(inc_dec_2_22b879e6_5_carry_barrow_out_8faccd5f), .Out(Out[9:8]),
    .Carry_Barrow_Out_8faccd5f(inc_dec_2_22b879e6_4_carry_barrow_out_8faccd5f));
  Inc_dec_2_22b879e6 inc_dec_2_22b879e6_5 (
    .Inc_Dec_32c9cf86(Inc_Dec_32c9cf86), .In(In[7:6]),
    .Carry_Barrow_In_ee85c3ba(inc_dec_2_22b879e6_6_carry_barrow_out_8faccd5f), .Out(Out[7:6]),
    .Carry_Barrow_Out_8faccd5f(inc_dec_2_22b879e6_5_carry_barrow_out_8faccd5f));
  Inc_dec_2_22b879e6 inc_dec_2_22b879e6_6 (
    .Inc_Dec_32c9cf86(Inc_Dec_32c9cf86), .In(In[5:4]),
    .Carry_Barrow_In_ee85c3ba(inc_dec_2_22b879e6_7_carry_barrow_out_8faccd5f), .Out(Out[5:4]),
    .Carry_Barrow_Out_8faccd5f(inc_dec_2_22b879e6_6_carry_barrow_out_8faccd5f));
  Inc_dec_2_22b879e6 inc_dec_2_22b879e6_7 (
    .Inc_Dec_32c9cf86(Inc_Dec_32c9cf86), .In(In[3:2]),
    .Carry_Barrow_In_ee85c3ba(inc_dec_2_22b879e6_8_carry_barrow_out_8faccd5f), .Out(Out[3:2]),
    .Carry_Barrow_Out_8faccd5f(inc_dec_2_22b879e6_7_carry_barrow_out_8faccd5f));
  Inc_dec_2_22b879e6 inc_dec_2_22b879e6_8 (
    .Inc_Dec_32c9cf86(Inc_Dec_32c9cf86), .In(In[1:0]), .Carry_Barrow_In_ee85c3ba(Carry_Barrow_In_ee85c3ba),
    .Out(Out[1:0]), .Carry_Barrow_Out_8faccd5f(inc_dec_2_22b879e6_8_carry_barrow_out_8faccd5f));
endmodule

module Inc_dec_8_1e64ec11 (
  input  [7:0] In,
  input  Inc_Dec_32c9cf86,
  input  Carry_Barrow_In_ee85c3ba,
  output Carry_Barrow_Out_8faccd5f,
  output [7:0] Out
);

  wire inc_dec_2_22b879e6_2_carry_barrow_out_8faccd5f, inc_dec_2_22b879e6_3_carry_barrow_out_8faccd5f,
       inc_dec_2_22b879e6_4_carry_barrow_out_8faccd5f;

  Inc_dec_2_22b879e6 inc_dec_2_22b879e6_1 (
    .Inc_Dec_32c9cf86(Inc_Dec_32c9cf86), .In(In[7:6]),
    .Carry_Barrow_In_ee85c3ba(inc_dec_2_22b879e6_2_carry_barrow_out_8faccd5f), .Out(Out[7:6]),
    .Carry_Barrow_Out_8faccd5f(Carry_Barrow_Out_8faccd5f));
  Inc_dec_2_22b879e6 inc_dec_2_22b879e6_2 (
    .Inc_Dec_32c9cf86(Inc_Dec_32c9cf86), .In(In[5:4]),
    .Carry_Barrow_In_ee85c3ba(inc_dec_2_22b879e6_3_carry_barrow_out_8faccd5f), .Out(Out[5:4]),
    .Carry_Barrow_Out_8faccd5f(inc_dec_2_22b879e6_2_carry_barrow_out_8faccd5f));
  Inc_dec_2_22b879e6 inc_dec_2_22b879e6_3 (
    .Inc_Dec_32c9cf86(Inc_Dec_32c9cf86), .In(In[3:2]),
    .Carry_Barrow_In_ee85c3ba(inc_dec_2_22b879e6_4_carry_barrow_out_8faccd5f), .Out(Out[3:2]),
    .Carry_Barrow_Out_8faccd5f(inc_dec_2_22b879e6_3_carry_barrow_out_8faccd5f));
  Inc_dec_2_22b879e6 inc_dec_2_22b879e6_4 (
    .Inc_Dec_32c9cf86(Inc_Dec_32c9cf86), .In(In[1:0]), .Carry_Barrow_In_ee85c3ba(Carry_Barrow_In_ee85c3ba),
    .Out(Out[1:0]), .Carry_Barrow_Out_8faccd5f(inc_dec_2_22b879e6_4_carry_barrow_out_8faccd5f));
endmodule

module Inc_dec_4_111c7295 (
  input  [3:0] In,
  input  Inc_Dec_32c9cf86,
  input  Carry_Barrow_In_ee85c3ba,
  output Carry_Barrow_Out_8faccd5f,
  output [3:0] Out
);

  wire inc_dec_2_22b879e6_2_carry_barrow_out_8faccd5f;

  Inc_dec_2_22b879e6 inc_dec_2_22b879e6_1 (
    .Inc_Dec_32c9cf86(Inc_Dec_32c9cf86), .In(In[3:2]),
    .Carry_Barrow_In_ee85c3ba(inc_dec_2_22b879e6_2_carry_barrow_out_8faccd5f), .Out(Out[3:2]),
    .Carry_Barrow_Out_8faccd5f(Carry_Barrow_Out_8faccd5f));
  Inc_dec_2_22b879e6 inc_dec_2_22b879e6_2 (
    .Inc_Dec_32c9cf86(Inc_Dec_32c9cf86), .In(In[1:0]), .Carry_Barrow_In_ee85c3ba(Carry_Barrow_In_ee85c3ba),
    .Out(Out[1:0]), .Carry_Barrow_Out_8faccd5f(inc_dec_2_22b879e6_2_carry_barrow_out_8faccd5f));
endmodule

module Inc_dec_2_22b879e6 (
  input  Inc_Dec_32c9cf86,
  input  [1:0] In,
  input  Carry_Barrow_In_ee85c3ba,
  output Carry_Barrow_Out_8faccd5f,
  output [1:0] Out
);

  wire not_1_out;
  wire [1:0] xnor_2_60bbe41c_1_y, xor_2_cfeac237_1_y;
  wire [1:1] nor_2_out;

  nor nor_1 (Carry_Barrow_Out_8faccd5f, xnor_2_60bbe41c_1_y[1], xnor_2_60bbe41c_1_y[0], not_1_out);
  nor nor_2 (nor_2_out[1], xnor_2_60bbe41c_1_y[0], not_1_out);
  XNor_2_60bbe41c xnor_2_60bbe41c_1 (.A(In), .B({2{Inc_Dec_32c9cf86}}), .Y(xnor_2_60bbe41c_1_y));
  not not_1 (not_1_out, Carry_Barrow_In_ee85c3ba);
  Xor_2_cfeac237 xor_2_cfeac237_1 (.A(In), .B({nor_2_out[1], Carry_Barrow_In_ee85c3ba}), .Y(xor_2_cfeac237_1_y));
  Error_to_Z_2_333e3e04 error_to_z_2_333e3e04_1 (.In(xor_2_cfeac237_1_y), .Out(Out));
endmodule

module Inc_dec_1_263ea2b8 (
  input  IncDec,
  input  In,
  input  Carry_Barrow_In_ee85c3ba,
  output Carry_Barrow_Out_8faccd5f,
  output Out
);

  wire and_1_out, and_2_out, and_3_out, and_4_out, not_1_out, not_2_out, not_3_out, not_4_out;

  not not_1 (not_1_out, IncDec);
  not not_2 (not_2_out, In);
  not not_3 (not_3_out, In);
  not not_4 (not_4_out, Carry_Barrow_In_ee85c3ba);
  and and_1 (and_1_out, not_1_out, In, Carry_Barrow_In_ee85c3ba);
  and and_2 (and_2_out, IncDec, not_2_out, Carry_Barrow_In_ee85c3ba);
  and and_3 (and_3_out, not_3_out, Carry_Barrow_In_ee85c3ba);
  and and_4 (and_4_out, In, not_4_out);
  or or_1 (Carry_Barrow_Out_8faccd5f, and_1_out, and_2_out);
  or or_2 (Out, and_3_out, and_4_out);
endmodule
