// Logisim project 8-1 Parity.circ as structural Verilog: 1 circuit, main circuit L_8_1_Parity_cb529c41
module L_8_1_Parity_cb529c41 (
  input  A,
  input  B,
  input  C,
  input  D,
  input  E,
  input  F,
  input  G,
  input  H,
  output Y
);

  wire xor_1_e881abe8_1_y, xor_1_e881abe8_2_y, xor_1_e881abe8_3_y, xor_1_e881abe8_4_y, xor_1_e881abe8_5_y,
       xor_1_e881abe8_6_y;

  Xor_1_e881abe8 xor_1_e881abe8_1 (.A(A), .B(B), .Y(xor_1_e881abe8_1_y));
  Xor_1_e881abe8 xor_1_e881abe8_2 (.A(C), .B(D), .Y(xor_1_e881abe8_2_y));
  Xor_1_e881abe8 xor_1_e881abe8_3 (.A(E), .B(F), .Y(xor_1_e881abe8_3_y));
  Xor_1_e881abe8 xor_1_e881abe8_4 (.A(G), .B(H), .Y(xor_1_e881abe8_4_y));
  Xor_1_e881abe8 xor_1_e881abe8_5 (.A(xor_1_e881abe8_1_y), .B(xor_1_e881abe8_2_y), .Y(xor_1_e881abe8_5_y));
  Xor_1_e881abe8 xor_1_e881abe8_6 (.A(xor_1_e881abe8_3_y), .B(xor_1_e881abe8_4_y), .Y(xor_1_e881abe8_6_y));
  Xor_1_e881abe8 xor_1_e881abe8_7 (.A(xor_1_e881abe8_5_y), .B(xor_1_e881abe8_6_y), .Y(Y));
endmodule
