// Logisim project Pulse Detect.circ as structural Verilog: 1 circuit, main circuit Pulse_Detect_78353950
module Pulse_Detect_78353950 (
  input  Clock,
  output Pulse
);

  wire not_1_out, not_2_out, not_3_out;

  not not_1 (not_1_out, Clock);
  not not_2 (not_2_out, not_1_out);
  not not_3 (not_3_out, not_2_out);
  and and_1 (Pulse, Clock, not_3_out);

  // Notes on the sheet:
  //   Rising Edge Detector:
  //   Pulse is too short to visually detect
  //   Simple demonstration possible via memory->Flip Flop
endmodule
