// Logisim project 4 bit Xor.circ as structural Verilog: 1 circuit, main circuit 4 bit Xor
module _4_bit_Xor (
  input  [3:0] A,
  input  [3:0] B,
  output [3:0] Y
);

  wire [3:0] and_1_out, and_2_out, not_1_out, not_2_out;

  assign not_1_out = ~A;  // NOT_Gate not_1, 4 bits wide
  assign not_2_out = ~B;  // NOT_Gate not_2, 4 bits wide
  assign and_1_out = not_1_out & B;  // AND_Gate and_1, 4 bits wide
  assign and_2_out = A & not_2_out;  // AND_Gate and_2, 4 bits wide
  assign Y = and_1_out | and_2_out;  // OR_Gate or_1, 4 bits wide
endmodule
