// Logisim project 8 bit Xor.circ as structural Verilog: 1 circuit, main circuit 8 bit Xor
module _8_bit_Xor (
  input  [7:0] A,
  input  [7:0] B,
  output [7:0] Y
);

  wire [7:0] and_1_out, and_2_out, not_1_out, not_2_out;

  assign not_1_out = ~A;  // NOT_Gate not_1, 8 bits wide
  assign and_1_out = not_1_out & B;  // AND_Gate and_1, 8 bits wide
  assign and_2_out = A & not_2_out;  // AND_Gate and_2, 8 bits wide
  assign not_2_out = ~B;  // NOT_Gate not_2, 8 bits wide
  assign Y = and_1_out | and_2_out;  // OR_Gate or_1, 8 bits wide
endmodule
