// Logisim project Xor.circ as structural Verilog: 5 circuits, main circuit Xor_1_e881abe8
module Xor_1_e881abe8 (
  input  A,
  input  B,
  output Y
);

  wire and_1_out, and_2_out, not_1_out, not_2_out;

  not not_1 (not_1_out, A);
  not not_2 (not_2_out, B);
  and and_1 (and_1_out, not_1_out, B);
  and and_2 (and_2_out, A, not_2_out);
  or or_1 (Y, and_1_out, and_2_out);
endmodule

module Xor_2_cfeac237 (
  input  [1:0] A,
  input  [1:0] B,
  output [1:0] Y
);

  wire [1:0] and_1_out, and_2_out, not_1_out, not_2_out;

  assign not_1_out = ~A;  // NOT_Gate not_1, 2 bits wide
  assign not_2_out = ~B;  // NOT_Gate not_2, 2 bits wide
  assign and_1_out = not_1_out & B;  // AND_Gate and_1, 2 bits wide
  assign and_2_out = A & not_2_out;  // AND_Gate and_2, 2 bits wide
  assign Y = and_1_out | and_2_out;  // OR_Gate or_1, 2 bits wide
endmodule

module Xor_4_2dfb8bb9 (
  input  [3:0] A,
  input  [3:0] B,
  output [3:0] Y
);

  wire [3:0] and_1_out, and_2_out, not_1_out, not_2_out;

  assign not_1_out = ~A;  // NOT_Gate not_1, 4 bits wide
  assign not_2_out = ~B;  // NOT_Gate not_2, 4 bits wide
  assign and_1_out = not_1_out & B;  // AND_Gate and_1, 4 bits wide
  assign and_2_out = A & not_2_out;  // AND_Gate and_2, 4 bits wide
  assign Y = and_1_out | and_2_out;  // OR_Gate or_1, 4 bits wide
endmodule

module Xor_8_4b3caf6e (
  input  [7:0] A,
  input  [7:0] B,
  output [7:0] Y
);

  wire [7:0] and_1_out, and_2_out, not_1_out, not_2_out;

  assign not_1_out = ~A;  // NOT_Gate not_1, 8 bits wide
  assign not_2_out = ~B;  // NOT_Gate not_2, 8 bits wide
  assign and_1_out = not_1_out & B;  // AND_Gate and_1, 8 bits wide
  assign and_2_out = A & not_2_out;  // AND_Gate and_2, 8 bits wide
  assign Y = and_1_out | and_2_out;  // OR_Gate or_1, 8 bits wide
endmodule

module Xor_16_31727c6d (
  input  [15:0] A,
  input  [15:0] B,
  output [15:0] Y
);

  wire [15:0] and_1_out, and_2_out, not_1_out, not_2_out;

  assign not_1_out = ~A;  // NOT_Gate not_1, 16 bits wide
  assign not_2_out = ~B;  // NOT_Gate not_2, 16 bits wide
  assign and_1_out = not_1_out & B;  // AND_Gate and_1, 16 bits wide
  assign and_2_out = A & not_2_out;  // AND_Gate and_2, 16 bits wide
  assign Y = and_1_out | and_2_out;  // OR_Gate or_1, 16 bits wide
endmodule
