// Logisim project 1 Bit Z Detector.circ as structural Verilog: 1 circuit, main circuit Z Detector
module Z_Detector (
  input  in_1,
  output out_2
);

  wire buffer_1_out, buffer_2_out;

  Xor xor_1 (.A(buffer_1_out), .B(buffer_2_out), .Y(out_2));
  buf buffer_1 (buffer_1_out, in_1);
  buf buffer_2 (buffer_2_out, in_1);
  Pull_Resistor #(.pull(1)) pull_resistor_1 (.node(buffer_2_out));
  Pull_Resistor pull_resistor_2 (.node(buffer_1_out));
endmodule
