// Logisim project Z Detector.circ as structural Verilog: 6 circuits, main circuit Z_Detector_1_be9a67f0
module Z_Detector_1_be9a67f0 (
  input  in_1,
  output out_2
);

  Pull_Circuit_c97a2554 pull_circuit_c97a2554_1 (.P_Down_914ca13e(in_1), .P_Up_984188f3(in_1), .out_3(out_2));
endmodule

module Z_Detector_2_fc4efac7 (
  input  [1:0] in_1,
  output [1:0] out_2
);

  Pull_Circuit_c97a2554 pull_circuit_c97a2554_1 (.P_Down_914ca13e(in_1[1]), .P_Up_984188f3(in_1[1]), .out_3(out_2[1]));
  Pull_Circuit_c97a2554 pull_circuit_c97a2554_2 (.P_Down_914ca13e(in_1[0]), .P_Up_984188f3(in_1[0]), .out_3(out_2[0]));
endmodule

module Z_Detector_4_aba5c6b5 (
  input  [3:0] in_1,
  output [3:0] out_2
);

  Pull_Circuit_c97a2554 pull_circuit_c97a2554_1 (.P_Down_914ca13e(in_1[3]), .P_Up_984188f3(in_1[3]), .out_3(out_2[3]));
  Pull_Circuit_c97a2554 pull_circuit_c97a2554_2 (.P_Down_914ca13e(in_1[2]), .P_Up_984188f3(in_1[2]), .out_3(out_2[2]));
  Pull_Circuit_c97a2554 pull_circuit_c97a2554_3 (.P_Down_914ca13e(in_1[1]), .P_Up_984188f3(in_1[1]), .out_3(out_2[1]));
  Pull_Circuit_c97a2554 pull_circuit_c97a2554_4 (.P_Down_914ca13e(in_1[0]), .P_Up_984188f3(in_1[0]), .out_3(out_2[0]));
endmodule

module Z_Detector_8_e7b9c500 (
  input  [7:0] in_1,
  output [7:0] out_2
);

  Pull_Circuit_c97a2554 pull_circuit_c97a2554_1 (.P_Down_914ca13e(in_1[6]), .P_Up_984188f3(in_1[6]), .out_3(out_2[6]));
  Pull_Circuit_c97a2554 pull_circuit_c97a2554_2 (.P_Down_914ca13e(in_1[7]), .P_Up_984188f3(in_1[7]), .out_3(out_2[7]));
  Pull_Circuit_c97a2554 pull_circuit_c97a2554_3 (.P_Down_914ca13e(in_1[5]), .P_Up_984188f3(in_1[5]), .out_3(out_2[5]));
  Pull_Circuit_c97a2554 pull_circuit_c97a2554_4 (.P_Down_914ca13e(in_1[4]), .P_Up_984188f3(in_1[4]), .out_3(out_2[4]));
  Pull_Circuit_c97a2554 pull_circuit_c97a2554_5 (.P_Down_914ca13e(in_1[3]), .P_Up_984188f3(in_1[3]), .out_3(out_2[3]));
  Pull_Circuit_c97a2554 pull_circuit_c97a2554_6 (.P_Down_914ca13e(in_1[2]), .P_Up_984188f3(in_1[2]), .out_3(out_2[2]));
  Pull_Circuit_c97a2554 pull_circuit_c97a2554_7 (.P_Down_914ca13e(in_1[1]), .P_Up_984188f3(in_1[1]), .out_3(out_2[1]));
  Pull_Circuit_c97a2554 pull_circuit_c97a2554_8 (.P_Down_914ca13e(in_1[0]), .P_Up_984188f3(in_1[0]), .out_3(out_2[0]));
endmodule

module Z_Detector_16_47ed8cfc (
  input  [15:0] in_1,
  output [15:0] out_2
);

  Pull_Circuit_c97a2554 pull_circuit_c97a2554_1 (
    .P_Down_914ca13e(in_1[15]), .P_Up_984188f3(in_1[15]), .out_3(out_2[15]));
  Pull_Circuit_c97a2554 pull_circuit_c97a2554_2 (
    .P_Down_914ca13e(in_1[13]), .P_Up_984188f3(in_1[13]), .out_3(out_2[13]));
  Pull_Circuit_c97a2554 pull_circuit_c97a2554_3 (
    .P_Down_914ca13e(in_1[14]), .P_Up_984188f3(in_1[14]), .out_3(out_2[14]));
  Pull_Circuit_c97a2554 pull_circuit_c97a2554_4 (
    .P_Down_914ca13e(in_1[12]), .P_Up_984188f3(in_1[12]), .out_3(out_2[12]));
  Pull_Circuit_c97a2554 pull_circuit_c97a2554_5 (
    .P_Down_914ca13e(in_1[11]), .P_Up_984188f3(in_1[11]), .out_3(out_2[11]));
  Pull_Circuit_c97a2554 pull_circuit_c97a2554_6 (
    .P_Down_914ca13e(in_1[10]), .P_Up_984188f3(in_1[10]), .out_3(out_2[10]));
  Pull_Circuit_c97a2554 pull_circuit_c97a2554_7 (.P_Down_914ca13e(in_1[9]), .P_Up_984188f3(in_1[9]), .out_3(out_2[9]));
  Pull_Circuit_c97a2554 pull_circuit_c97a2554_8 (.P_Down_914ca13e(in_1[8]), .P_Up_984188f3(in_1[8]), .out_3(out_2[8]));
  Pull_Circuit_c97a2554 pull_circuit_c97a2554_9 (.P_Down_914ca13e(in_1[7]), .P_Up_984188f3(in_1[7]), .out_3(out_2[7]));
  Pull_Circuit_c97a2554 pull_circuit_c97a2554_10 (.P_Down_914ca13e(in_1[6]), .P_Up_984188f3(in_1[6]), .out_3(out_2[6]));
  Pull_Circuit_c97a2554 pull_circuit_c97a2554_11 (.P_Down_914ca13e(in_1[5]), .P_Up_984188f3(in_1[5]), .out_3(out_2[5]));
  Pull_Circuit_c97a2554 pull_circuit_c97a2554_12 (.P_Down_914ca13e(in_1[4]), .P_Up_984188f3(in_1[4]), .out_3(out_2[4]));
  Pull_Circuit_c97a2554 pull_circuit_c97a2554_13 (.P_Down_914ca13e(in_1[3]), .P_Up_984188f3(in_1[3]), .out_3(out_2[3]));
  Pull_Circuit_c97a2554 pull_circuit_c97a2554_14 (.P_Down_914ca13e(in_1[2]), .P_Up_984188f3(in_1[2]), .out_3(out_2[2]));
  Pull_Circuit_c97a2554 pull_circuit_c97a2554_15 (.P_Down_914ca13e(in_1[1]), .P_Up_984188f3(in_1[1]), .out_3(out_2[1]));
  Pull_Circuit_c97a2554 pull_circuit_c97a2554_16 (.P_Down_914ca13e(in_1[0]), .P_Up_984188f3(in_1[0]), .out_3(out_2[0]));
endmodule

module Pull_Circuit_c97a2554 (
  input  P_Down_914ca13e,
  input  P_Up_984188f3,
  output out_3
);

  Xor_1_e881abe8 xor_1_e881abe8_1 (.A(P_Down_914ca13e), .B(P_Up_984188f3), .Y(out_3));

  // Notes on the sheet:
  //   P_Down_914ca13e: pull=down
  //   P_Up_984188f3: pull=up
endmodule
