// Logisim project 1-4 Extender.circ as structural Verilog: 1 circuit, main circuit L_1_4_Bit_extender_dc7f6f84
module L_1_4_Bit_extender_dc7f6f84 (
  input  A,
  output [3:0] Y
);


  assign Y = {3'b000, A};
endmodule
