// Logisim project 1-8 Extender.circ as structural Verilog: 1 circuit, main circuit L_1_8_Bit_extender_8f3d069e
module L_1_8_Bit_extender_8f3d069e (
  input  A,
  output [7:0] Y
);


  assign Y = {{7{1'b0}}, A};
endmodule
