// Logisim project Bit Extender (1).circ as structural Verilog: 4 circuits, main circuit L_1_bit_extender_16_340f34d4
module L_1_bit_extender_16_340f34d4 (
  input  A,
  output [15:0] Y
);


  assign Y = {{15{1'b0}}, A};
endmodule

module L_1_bit_extender_8_e90924a2 (
  input  A,
  output [7:0] Y
);


  assign Y = {{7{1'b0}}, A};
endmodule

module L_1_bit_extender_4_9252b35c (
  input  A,
  output [3:0] Y
);


  assign Y = {3'b000, A};
endmodule

module L_1_bit_extender_2_65176f40 (
  input  A,
  output [1:0] Y
);


  assign Y = {1'b0, A};
endmodule
