// Logisim project Bit Extender (2).circ as structural Verilog: 3 circuits, main circuit L_2_bit_extender_16_8e03a419
module L_2_bit_extender_16_8e03a419 (
  input  [1:0] A,
  output [15:0] Y
);


  assign Y = {{14{1'b0}}, A};
endmodule

module L_2_bit_extender_8_94620cb2 (
  input  [1:0] A,
  output [7:0] Y
);


  assign Y = {{6{1'b0}}, A};
endmodule

module L_2_bit_extender_4_eedec326 (
  input  [1:0] A,
  output [3:0] Y
);


  assign Y = {2'b00, A};
endmodule
