// Logisim project Bit Extender (4).circ as structural Verilog: 2 circuits, main circuit L_4_bit_extender_16_8d5a9793
module L_4_bit_extender_16_8d5a9793 (
  input  [3:0] A,
  output [15:0] Y
);


  assign Y = {{12{1'b0}}, A};
endmodule

module L_4_bit_extender_8_627adc9d (
  input  [3:0] A,
  output [7:0] Y
);


  assign Y = {4'b0000, A};
endmodule
