// Logisim project Bit Extender (8).circ as structural Verilog: 1 circuit, main circuit L_8_bit_extender_16_22419d45
module L_8_bit_extender_16_22419d45 (
  input  [7:0] A,
  output [15:0] Y
);


  assign Y = {{8{1'b0}}, A};
endmodule
