// Logisim project CPU.circ as structural Verilog: 7 circuits, main circuit Main
module Pin_check_669b1847 (
  input  [7:0] in_1,
  input  [15:0] in_2,
  input  in_3,
  input  in_4,
  input  in_5
);

  wire main_1_d2, main_1_d3, main_1_d4, main_1_d5, main_1_out_26, main_1_out_27, main_1_out_32, main_1_out_33;

  Main main_1 (
    .D7(main_1_out_26), .D6(main_1_out_27), .in_3(main_1_d5), .in_4(main_1_d4), .in_5(main_1_d3),
    .in_6(main_1_d2), .D1(main_1_out_32), .D0(main_1_out_33), .out_26(main_1_out_26), .out_27(main_1_out_27),
    .D5(main_1_d5), .D4(main_1_d4), .D3(main_1_d3), .D2(main_1_d2), .out_32(main_1_out_32),
    .out_33(main_1_out_33));  // open: Vss, Vbb, Vcc, Vdd, Mux, Read, Write, INTE, Inc_Dec_16fb1df5, Hold, Read_Write_Mem_af0c671a, Ready, Phase1, Instr_Register_Write_6a82d22d, Phase2, Reset, Read_Write_into_Register_e18d31a4, WR, DBIN, INT, HLDA, Wait, Sync, A15, A14, A13, A12, A11, A10, A9, A8, A7, A6, A5, A4, A3, A2, A1, A0
  RAM #(.addrWidth(16)) ram_1 (.addr(in_2), .data(in_1), .sel(in_5), .clk(in_4), .ld(in_3));  // open: clr
endmodule

module Main (
  input  D7,
  input  D6,
  input  in_3,
  input  in_4,
  input  in_5,
  input  in_6,
  input  D1,
  input  D0,
  input  Inc_Dec_16fb1df5,
  input  [3:0] Read,
  input  [3:0] Mux,
  input  [3:0] Write,
  input  Read_Write_Mem_af0c671a,
  input  Instr_Register_Write_6a82d22d,
  input  Read_Write_into_Register_e18d31a4,
  input  Vss,
  input  Vbb,
  input  Vcc,
  input  Vdd,
  input  INTE,
  input  Phase2,
  input  Hold,
  input  Ready,
  input  Phase1,
  input  Reset,
  output out_26,
  output out_27,
  output D5,
  output D4,
  output D3,
  output D2,
  output out_32,
  output out_33,
  output A15,
  output A14,
  output A13,
  output A12,
  output A11,
  output A10,
  output A9,
  output A8,
  output A7,
  output A6,
  output A5,
  output A4,
  output A3,
  output A2,
  output A1,
  output A0,
  output WR,
  output HLDA,
  output Wait,
  output Sync,
  output DBIN,
  output INT
);

  wire and_1_out, Clock, l_3_8_decoder_c117a043_1_y2, l_3_8_decoder_c117a043_1_y4,
       l_3_8_decoder_c117a043_1_y5, l_3_8_decoder_c117a043_1_y6;
  wire [0:0] timing_and_control_36376d52_1_registry_control_fe15185c;
  wire [1:0] timing_and_control_36376d52_1_en_right_aba74a23_2;
  wire [2:0] timing_and_control_36376d52_1_en_left_9b905a13;
  wire [3:0] timing_and_control_36376d52_1_alu_control_cffb97c3,
       timing_and_control_36376d52_1_registry_control_fe15185c_2,
       timing_and_control_36376d52_1_registry_control_fe15185c_3,
       timing_and_control_36376d52_1_registry_control_fe15185c_4;
  wire [6:0] timing_and_control_36376d52_1_en_right_aba74a23;
  wire [7:0] alu_1_flag_out, alu_1_result, controlled_buffer_1_out, controlled_buffer_2_out,
       controlled_buffer_3_out, controlled_buffer_6_out, E1, E2, E3, E4, E5, E6,
       scratch_pad_49ad1382_1_bus_out;
  wire [15:0] scratch_pad_49ad1382_1_mem_bus;

  assign controlled_buffer_1_out = l_3_8_decoder_c117a043_1_y4 ? controlled_buffer_3_out : 8'bz;  // Controlled_Buffer controlled_buffer_1
  CPU_Register_a8a89204 cpu_register_a8a89204_1 (.Clk(Clock), .In(controlled_buffer_1_out), .Out(E1));  // open: En
  assign controlled_buffer_2_out = l_3_8_decoder_c117a043_1_y5 ? controlled_buffer_3_out : 8'bz;  // Controlled_Buffer controlled_buffer_2
  CPU_Register_a8a89204 cpu_register_a8a89204_2 (.Clk(Clock), .In(controlled_buffer_2_out), .Out(E3));  // open: En
  Accumulator_Latch_684198f5 accumulator_latch_684198f5_1 (.In(E1), .Out(E2));  // open: Clk
  CPU_Register_a8a89204 cpu_register_a8a89204_3 (.Clk(Clock), .In(alu_1_flag_out), .Out(E4));  // open: En
  ALU alu_1 (
    .A(E2), .B(E3), .Result(alu_1_result), .Flag_in(E4), .Flag_Out(alu_1_flag_out),
    .OpCode(timing_and_control_36376d52_1_alu_control_cffb97c3));
  assign controlled_buffer_3_out = l_3_8_decoder_c117a043_1_y2 ? E4 : 8'bz;  // Controlled_Buffer controlled_buffer_3
  assign controlled_buffer_3_out = l_3_8_decoder_c117a043_1_y6 ? alu_1_result : 8'bz;  // Controlled_Buffer controlled_buffer_4
  L_3_8_Decoder_c117a043 l_3_8_decoder_c117a043_1 (
    .En(1'b1), .Select(timing_and_control_36376d52_1_en_left_9b905a13), .y2(l_3_8_decoder_c117a043_1_y2),
    .y4(l_3_8_decoder_c117a043_1_y4), .y5(l_3_8_decoder_c117a043_1_y5), .y6(l_3_8_decoder_c117a043_1_y6));  // open: y1, y3, y7, y0
  and and_1 (and_1_out, ~Vss, ~Vbb, Vcc, Vdd);  // AND_Gate
  Dual_CPU_Buffer_da751fdb dual_cpu_buffer_da751fdb_1 (
    .In0({D7, D6, in_3, in_4, in_5, in_6, D1, D0}), .In1(controlled_buffer_3_out),
    .Direction(timing_and_control_36376d52_1_en_right_aba74a23[6]),
    .En(timing_and_control_36376d52_1_en_right_aba74a23_2), .Out0(controlled_buffer_3_out),
    .Out1({D7, D6, in_3, in_4, in_5, in_6, D1, D0}));
  Timing_and_Control_36376d52 timing_and_control_36376d52_1 (
    .INTE(INTE), .Hold(Hold), .Reg_Control_In_7aa28bf8({Mux, Read, Write, Inc_Dec_16fb1df5}), .Ready(Ready),
    .Reset(Reset), .Ph1(Phase1), .Ph2(Phase2),
    .Read_from_Register_79ba4f29(Read_Write_into_Register_e18d31a4),
    .Read_Write_Memory_ff29de52(Read_Write_Mem_af0c671a),
    .Write_Instruction_Register_d2f0dade(Instr_Register_Write_6a82d22d), .En(and_1_out), .out_22(INT),
    .Hold_Ack_164ef7dd(HLDA), .ALU_Control_cffb97c3(timing_and_control_36376d52_1_alu_control_cffb97c3),
    .Registry_Control_fe15185c({timing_and_control_36376d52_1_registry_control_fe15185c_4, timing_and_control_36376d52_1_registry_control_fe15185c_3, timing_and_control_36376d52_1_registry_control_fe15185c_2, timing_and_control_36376d52_1_registry_control_fe15185c[0]}),
    .Wait(Wait),
    .En_Right_aba74a23({timing_and_control_36376d52_1_en_right_aba74a23[6], timing_and_control_36376d52_1_en_right_aba74a23_2, timing_and_control_36376d52_1_en_right_aba74a23[3:0]}),
    .En_Left_9b905a13(timing_and_control_36376d52_1_en_left_9b905a13), .Sync(Sync), .L_WR_976b5940(WR),
    .Clk(Clock), .DBIN(DBIN));
  CPU_Register_a8a89204 cpu_register_a8a89204_4 (
    .En(timing_and_control_36376d52_1_en_right_aba74a23[2]), .Clk(Clock), .In(controlled_buffer_3_out),
    .Out(E5));
  Instruction_Encoder_3db71ec6 instruction_encoder_3db71ec6_1 (.Data_In_9342ff20(E5));  // open: V, Encoded_Instruction_Group_74c432e9
  // Probe on controlled_buffer_3_out
  assign controlled_buffer_3_out = timing_and_control_36376d52_1_en_right_aba74a23[1] ? scratch_pad_49ad1382_1_bus_out : 8'bz;  // Controlled_Buffer controlled_buffer_5
  assign controlled_buffer_6_out = timing_and_control_36376d52_1_en_right_aba74a23[1] ? controlled_buffer_3_out : 8'bz;  // Controlled_Buffer controlled_buffer_6
  Scratch_Pad_49ad1382 scratch_pad_49ad1382_1 (
    .Read_Select(timing_and_control_36376d52_1_registry_control_fe15185c_3),
    .Write_Select(timing_and_control_36376d52_1_registry_control_fe15185c_2),
    .Bus_Read_Write(timing_and_control_36376d52_1_registry_control_fe15185c_4),
    .Bus_In(controlled_buffer_6_out),
    .Increment_Decrement(timing_and_control_36376d52_1_registry_control_fe15185c[0]), .Clock(Clock),
    .Mem_Bus(scratch_pad_49ad1382_1_mem_bus), .Bus_Out(scratch_pad_49ad1382_1_bus_out), .Error(E6));
  assign {A15, A14, A13, A12, A11, A10, A9, A8, A7, A6, A5, A4, A3, A2, A1, A0} = timing_and_control_36376d52_1_en_right_aba74a23[0] ? scratch_pad_49ad1382_1_mem_bus : 16'bz;  // Controlled_Buffer controlled_buffer_7

  assign D2 = in_6;
  assign D3 = in_5;
  assign D4 = in_4;
  assign D5 = in_3;
  assign out_26 = D7;
  assign out_27 = D6;
  assign out_32 = D1;
  assign out_33 = D0;

  // Notes on the sheet:
  //   Reset: pull=down
  //   Any red lines here means Logisim has failed to load a register
endmodule

// Register
module CPU_Register_a8a89204 (
  input  En,
  input  Clk,
  input  [7:0] In,
  output [7:0] Out
);

  Register_8_252a90b2 register_8_252a90b2_1 (.In(In), .W(En), .Clk(Clk), .Out(Out));  // open: Clear
endmodule

module Dual_CPU_Buffer_da751fdb (
  input  [1:0] En,
  input  [7:0] In0,
  input  [7:0] In1,
  input  Direction,
  output [7:0] Out0,
  output [7:0] Out1
);

  wire [7:0] l_2_1_demux_8_2e02d5b2_1_l_0_f163cde3, l_2_1_demux_8_2e02d5b2_1_l_1_507cfd33,
       latch_register_8_dfa3016f_1_out, mux_8_1_y;

  Mux_8 mux_8_1 (.p0(In0), .p1(In1), .Select(Direction), .Y(mux_8_1_y));
  Latch_Register_8_dfa3016f latch_register_8_dfa3016f_1 (
    .In(mux_8_1_y), .W(En[1]), .Out(latch_register_8_dfa3016f_1_out));  // open: Clear
  L_2_1_Demux_8_2e02d5b2 l_2_1_demux_8_2e02d5b2_1 (
    .Select(Direction), .Y(latch_register_8_dfa3016f_1_out),
    .L_0_f163cde3(l_2_1_demux_8_2e02d5b2_1_l_0_f163cde3), .L_1_507cfd33(l_2_1_demux_8_2e02d5b2_1_l_1_507cfd33));
  assign Out0 = En[0] ? l_2_1_demux_8_2e02d5b2_1_l_0_f163cde3 : 8'bz;  // Controlled_Buffer controlled_buffer_1
  assign Out1 = En[0] ? l_2_1_demux_8_2e02d5b2_1_l_1_507cfd33 : 8'bz;  // Controlled_Buffer controlled_buffer_2

  // Notes on the sheet:
  //   En: pull=down
  //   0 is from top
  //   1 is from bottom
endmodule

module Accumulator_Latch_684198f5 (
  input  [7:0] In,
  input  Clk,
  output [7:0] Out
);

  wire d_latch_3f9c06d7_1_p2, not_1_out, z_detector_1_be9a67f0_1_out_2;

  Z_Detector_1_be9a67f0 z_detector_1_be9a67f0_1 (.in_1(In[7]), .out_2(z_detector_1_be9a67f0_1_out_2));
  not not_1 (not_1_out, z_detector_1_be9a67f0_1_out_2);
  // D_Latch_3f9c06d7 d_latch_3f9c06d7_1: pin names not known; wires that end beside it: In[0], d_latch_3f9c06d7_1_p2, Out[0]
  // D_Latch_3f9c06d7 d_latch_3f9c06d7_2: pin names not known; wires that end beside it: In[1], d_latch_3f9c06d7_1_p2, d_latch_3f9c06d7_1_p2, Out[1]
  // D_Latch_3f9c06d7 d_latch_3f9c06d7_3: pin names not known; wires that end beside it: In[2], d_latch_3f9c06d7_1_p2, d_latch_3f9c06d7_1_p2, Out[2]
  // D_Latch_3f9c06d7 d_latch_3f9c06d7_4: pin names not known; wires that end beside it: In[3], d_latch_3f9c06d7_1_p2, d_latch_3f9c06d7_1_p2, Out[3]
  // D_Latch_3f9c06d7 d_latch_3f9c06d7_5: pin names not known; wires that end beside it: In[4], d_latch_3f9c06d7_1_p2, d_latch_3f9c06d7_1_p2, Out[4]
  // D_Latch_3f9c06d7 d_latch_3f9c06d7_6: pin names not known; wires that end beside it: In[5], d_latch_3f9c06d7_1_p2, d_latch_3f9c06d7_1_p2, Out[5]
  // D_Latch_3f9c06d7 d_latch_3f9c06d7_7: pin names not known; wires that end beside it: In[6], d_latch_3f9c06d7_1_p2, d_latch_3f9c06d7_1_p2, Out[6]
  D_Latch_3f9c06d7 d_latch_3f9c06d7_8 (.Data(In[7]), .En(d_latch_3f9c06d7_1_p2), .Output(Out[7]));  // open: Clear
  and and_1 (d_latch_3f9c06d7_1_p2, not_1_out, Clk);

  // Notes on the sheet:
  //   Clk: pull=down
endmodule

module Timing_and_Control_36376d52 (
  input  Read_from_Register_79ba4f29,
  input  Read_Write_Memory_ff29de52,
  input  Write_Instruction_Register_d2f0dade,
  input  Reset,
  input  En,
  input  [12:0] Reg_Control_In_7aa28bf8,
  input  INTE,
  input  Ph2,
  input  Hold,
  input  Ready,
  input  Ph1,
  output [2:0] En_Left_9b905a13,
  output [6:0] En_Right_aba74a23,
  output Clk,
  output [3:0] ALU_Control_cffb97c3,
  output [12:0] Registry_Control_fe15185c,
  output L_WR_976b5940,
  output Hold_Ack_164ef7dd,
  output Wait,
  output Sync,
  output DBIN,
  output out_22
);

  Clock clock_1 (.out(Clk));

  assign ALU_Control_cffb97c3 = 4'b0000;
  assign DBIN = 1'b0;
  assign En_Left_9b905a13 = 3'b000;
  assign {En_Right_aba74a23[6:4], En_Right_aba74a23[2:0]} = {{3{Read_Write_Memory_ff29de52}}, Write_Instruction_Register_d2f0dade, Read_from_Register_79ba4f29, Read_Write_Memory_ff29de52};
  assign Hold_Ack_164ef7dd = 1'b0;
  assign L_WR_976b5940 = 1'b0;
  assign out_22 = 1'b0;
  assign Registry_Control_fe15185c = Reg_Control_In_7aa28bf8;
  assign Sync = 1'b0;
  assign Wait = 1'b0;

  // Other names for the same wires on the sheet: Read_Write_Bus_e09188bf[3:0] = Reg_Control_In_7aa28bf8[3:0];
  //   Read[3:0] = Reg_Control_In_7aa28bf8[7:4]; Write[3:0] = Reg_Control_In_7aa28bf8[11:8];
  //   Increment_decrement_5d92e906 = Reg_Control_In_7aa28bf8[12]

  // Notes on the sheet:
  //   En_Right_aba74a23: pull=down
  //   En_Left_9b905a13: pull=down
  //   Read_from_Register_79ba4f29: pull=down
  //   Read_Write_Memory_ff29de52: pull=down
  //   Write_Instruction_Register_d2f0dade: pull=down
  //   En: pull=down
  //   4 Enable latch read
  //   5 Enable latch write
  //   6 Direction of Bus Latch
  //   0 Memory Bus 1: Register Buffer
  //   2 Instruction Register
endmodule

module Instruction_Decoder_and_Machine_Cycle_Encoding_a12fe81e (
  input  [7:0] Data_In_e17823f7,
  output Bus_Read_d634b182,
  output Bus_Write_c92d50ce,
  output [3:0] Increment_Decrement_2860f9a1
);

  wire [4:0] instruction_encoder_3db71ec6_1_encoded_instruction_group_74c432e9;

  Instruction_Encoder_3db71ec6 instruction_encoder_3db71ec6_1 (
    .Data_In_9342ff20(8'hc4),
    .Encoded_Instruction_Group_74c432e9(instruction_encoder_3db71ec6_1_encoded_instruction_group_74c432e9));  // open: V
  // Probe on instruction_encoder_3db71ec6_1_encoded_instruction_group_74c432e9
endmodule
