// Logisim project Instruction Encoder.circ as structural Verilog: 1 circuit, main circuit Instruction_Encoder_3db71ec6
module Instruction_Encoder_3db71ec6 (
  input  [7:0] Data_In_9342ff20,
  output V,
  output [4:0] Encoded_Instruction_Group_74c432e9
);

  wire [3:0] undriven_15, undriven_22;
  wire [3:3] undriven_14, undriven_16, undriven_21;
  wire [4:0] undriven_17, undriven_18;
  wire [4:3] undriven_19, undriven_20;
  wire [4:4] undriven_10, undriven_11, undriven_12, undriven_13;
  wire [5:0] undriven_7, undriven_24, undriven_25;
  wire [5:3] undriven, undriven_2, undriven_3, undriven_4, undriven_8;
  wire [5:4] undriven_5, undriven_6, undriven_9, undriven_23;
  wire [31:0] equals_8_f6a9e01b_32_y;

  Equals_8_f6a9e01b equals_8_f6a9e01b_1 (.B(8'hcd), .A(Data_In_9342ff20), .Y(equals_8_f6a9e01b_32_y[30]));
  Equals_8_f6a9e01b equals_8_f6a9e01b_2 (.B(8'hc9), .A(Data_In_9342ff20), .Y(equals_8_f6a9e01b_32_y[31]));
  L_32_5_Priority_Encoder_c1276c5e l_32_5_priority_encoder_c1276c5e_1 (
    .in_1(equals_8_f6a9e01b_32_y), .Out(Encoded_Instruction_Group_74c432e9), .V(V));
  Equals_8_f6a9e01b equals_8_f6a9e01b_3 (
    .B({2'b11, undriven, 3'b000}), .A(Data_In_9342ff20), .Y(equals_8_f6a9e01b_32_y[29]));
  Equals_8_f6a9e01b equals_8_f6a9e01b_4 (
    .B({2'b11, undriven_2, 3'b100}), .A(Data_In_9342ff20), .Y(equals_8_f6a9e01b_32_y[28]));
  Equals_8_f6a9e01b equals_8_f6a9e01b_5 (
    .B({2'b11, undriven_3, 3'b010}), .A(Data_In_9342ff20), .Y(equals_8_f6a9e01b_32_y[27]));
  Equals_8_f6a9e01b equals_8_f6a9e01b_6 (.B(8'hc3), .A(Data_In_9342ff20), .Y(equals_8_f6a9e01b_32_y[26]));
  Equals_8_f6a9e01b equals_8_f6a9e01b_7 (.B(8'he9), .A(Data_In_9342ff20), .Y(equals_8_f6a9e01b_32_y[25]));
  Equals_8_f6a9e01b equals_8_f6a9e01b_8 (.B(8'h76), .A(Data_In_9342ff20), .Y(equals_8_f6a9e01b_32_y[24]));
  Equals_8_f6a9e01b equals_8_f6a9e01b_9 (
    .B({2'b11, undriven_4, 3'b111}), .A(Data_In_9342ff20), .Y(equals_8_f6a9e01b_32_y[23]));
  Equals_8_f6a9e01b equals_8_f6a9e01b_10 (
    .B({2'b11, undriven_5, 4'b0001}), .A(Data_In_9342ff20), .Y(equals_8_f6a9e01b_32_y[22]));
  Equals_8_f6a9e01b equals_8_f6a9e01b_11 (
    .B({2'b11, undriven_6, 4'b0101}), .A(Data_In_9342ff20), .Y(equals_8_f6a9e01b_32_y[21]));
  Equals_8_f6a9e01b equals_8_f6a9e01b_12 (.B({8{1'b0}}), .A(Data_In_9342ff20), .Y(equals_8_f6a9e01b_32_y[20]));
  Equals_8_f6a9e01b equals_8_f6a9e01b_13 (
    .B({2'b01, undriven_7}), .A(Data_In_9342ff20), .Y(equals_8_f6a9e01b_32_y[19]));
  Equals_8_f6a9e01b equals_8_f6a9e01b_14 (
    .B({2'b00, undriven_8, 3'b110}), .A(Data_In_9342ff20), .Y(equals_8_f6a9e01b_32_y[18]));
  Equals_8_f6a9e01b equals_8_f6a9e01b_15 (
    .B({2'b00, undriven_9, 4'b0001}), .A(Data_In_9342ff20), .Y(equals_8_f6a9e01b_32_y[17]));
  Equals_8_f6a9e01b equals_8_f6a9e01b_16 (
    .B({3'b000, undriven_10[4], 4'b0010}), .A(Data_In_9342ff20), .Y(equals_8_f6a9e01b_32_y[16]));
  Equals_8_f6a9e01b equals_8_f6a9e01b_17 (
    .B({3'b000, undriven_11[4], 4'b1010}), .A(Data_In_9342ff20), .Y(equals_8_f6a9e01b_32_y[15]));
  Equals_8_f6a9e01b equals_8_f6a9e01b_18 (
    .B({3'b001, undriven_12[4], 4'b0010}), .A(Data_In_9342ff20), .Y(equals_8_f6a9e01b_32_y[14]));
  Equals_8_f6a9e01b equals_8_f6a9e01b_19 (
    .B({3'b001, undriven_13[4], 4'b1010}), .A(Data_In_9342ff20), .Y(equals_8_f6a9e01b_32_y[13]));
  Equals_8_f6a9e01b equals_8_f6a9e01b_20 (
    .B({4'b1111, undriven_14[3], 3'b011}), .A(Data_In_9342ff20), .Y(equals_8_f6a9e01b_32_y[12]));
  Equals_8_f6a9e01b equals_8_f6a9e01b_21 (.B(8'heb), .A(Data_In_9342ff20), .Y(equals_8_f6a9e01b_32_y[11]));
  Equals_8_f6a9e01b equals_8_f6a9e01b_22 (
    .B({4'b1001, undriven_15}), .A(Data_In_9342ff20), .Y(equals_8_f6a9e01b_32_y[10]));
  Equals_8_f6a9e01b equals_8_f6a9e01b_23 (
    .B({3'b101, undriven_17}), .A(Data_In_9342ff20), .Y(equals_8_f6a9e01b_32_y[8]));
  Equals_8_f6a9e01b equals_8_f6a9e01b_24 (
    .B({4'b1101, undriven_16[3], 3'b110}), .A(Data_In_9342ff20), .Y(equals_8_f6a9e01b_32_y[9]));
  Equals_8_f6a9e01b equals_8_f6a9e01b_25 (
    .B({3'b111, undriven_18}), .A(Data_In_9342ff20), .Y(equals_8_f6a9e01b_32_y[7]));
  Equals_8_f6a9e01b equals_8_f6a9e01b_26 (
    .B({3'b000, undriven_19, 3'b111}), .A(Data_In_9342ff20), .Y(equals_8_f6a9e01b_32_y[6]));
  Equals_8_f6a9e01b equals_8_f6a9e01b_27 (
    .B({3'b001, undriven_20, 3'b111}), .A(Data_In_9342ff20), .Y(equals_8_f6a9e01b_32_y[5]));
  Equals_8_f6a9e01b equals_8_f6a9e01b_28 (
    .B({4'b1101, undriven_21[3], 3'b011}), .A(Data_In_9342ff20), .Y(equals_8_f6a9e01b_32_y[4]));
  Equals_8_f6a9e01b equals_8_f6a9e01b_29 (
    .B({4'b1000, undriven_22}), .A(Data_In_9342ff20), .Y(equals_8_f6a9e01b_32_y[3]));
  Equals_8_f6a9e01b equals_8_f6a9e01b_30 (
    .B({2'b00, undriven_23, 4'b1001}), .A(Data_In_9342ff20), .Y(equals_8_f6a9e01b_32_y[2]));
  Equals_8_f6a9e01b equals_8_f6a9e01b_31 (
    .B({2'b00, undriven_24}), .A(Data_In_9342ff20), .Y(equals_8_f6a9e01b_32_y[1]));
  Equals_8_f6a9e01b equals_8_f6a9e01b_32 (
    .B({2'b11, undriven_25}), .A(Data_In_9342ff20), .Y(equals_8_f6a9e01b_32_y[0]));

  // Notes on the sheet:
  //   4
  //   8
  //   12
  //   16
  //   20
  //   24
  //   28
  //   32
endmodule
