// Logisim project Scratch Pad.circ as structural Verilog: 1 circuit, main circuit Scratch_Pad_49ad1382
module Scratch_Pad_49ad1382 (
  input  Increment_Decrement,
  input  [3:0] Bus_Read_Write,
  input  [7:0] Bus_In,
  input  Clock,
  input  [3:0] Read_Select,
  input  [3:0] Write_Select,
  output [7:0] Bus_Out,
  output [7:0] Error,
  output [15:0] Mem_Bus
);

  wire not_2_out, not_3_out, not_6_out, not_7_out, z_detector_1_be9a67f0_1_out_2,
       z_detector_1_be9a67f0_2_out_2;
  wire [2:0] not_1_out, not_5_out;
  wire [3:0] Write_Select_t;
  wire [3:3] not_1_out_2, not_5_out_2;
  wire [7:0] B, C, controlled_buffer_2_out, controlled_buffer_5_out, D, E, H, inc_dec_8_1e64ec11_1_out, L,
       mux_8_1_out_10, mux_8_2_out_10, Read_8, Write_8, Write_B, Write_BC_Pair, Write_D, Write_DE_Pair,
       Write_H, Write_HL_Pair, Write_W, Write_WZ_Pair;
  wire [15:0] Addr_Load, controlled_buffer_4_out, inc_dec_16_1df549c4_1_out, mux_16_1_o, PC, Read_16,
       Read_WZ_Pair, Stack, Write_16, Write_PC, Write_Stack, z_detector_16_47ed8cfc_1_out_2;

  Pull_Resistor pull_resistor_1 (.node(Read_8));
  assign Read_8 = not_2_out ? mux_8_1_out_10 : 8'bz;  // Controlled_Buffer controlled_buffer_1
  Mux_8 mux_8_1 (
    .in_9(not_1_out), .p4(H), .p5(L), .p6(Read_WZ_Pair[15:8]), .p7(Read_WZ_Pair[7:0]), .p0(B), .p1(C),
    .p2(D), .p3(E), .out_10(mux_8_1_out_10));
  assign controlled_buffer_2_out = not_3_out ? Write_8 : 8'bz;  // Controlled_Buffer controlled_buffer_2
  L_8_1_Demux_8_58d4daa4 l_8_1_demux_8_58d4daa4_1 (
    .in_2(Write_Select_t[2:0]), .Y(controlled_buffer_2_out), .L_2_9682dceb(Write_D),
    .L_3_c2e8e44e(Write_DE_Pair), .L_4_5ba2c680(Write_H), .L_0_5ac68a80(Write_B),
    .L_5_c7845d74(Write_HL_Pair), .L_6_a1ac0909(Write_W), .L_7_4b7fadd1(Write_WZ_Pair),
    .L_1_ab49ad53(Write_BC_Pair));
  assign {not_1_out_2[3], not_1_out} = ~Read_Select;  // NOT_Gate not_1, 4 bits wide
  not not_2 (not_2_out, not_1_out_2[3]);
  not not_3 (not_3_out, Write_Select_t[3]);
  Register_16_2fb72861 register_16_2fb72861_1 (.W(1'b1), .In(Addr_Load), .Clk(Clock), .Out(Mem_Bus));  // open: Clear
  Pull_Resistor pull_resistor_2 (.node(Read_16));
  assign Read_16 = not_1_out_2[3] ? mux_16_1_o : 16'bz;  // Controlled_Buffer controlled_buffer_3
  Mux_16 mux_16_1 (
    .p2({D, E}), .p3(Stack), .p4({H, L}), .p0({B, C}), .p1(PC), .s(not_1_out), .p5(Mem_Bus),
    .p6(Read_WZ_Pair), .o(mux_16_1_o));  // open: p7
  assign controlled_buffer_4_out = Write_Select_t[3] ? Write_16 : 16'bz;  // Controlled_Buffer controlled_buffer_4
  L_8_1_Demux_16_5be8a8cb l_8_1_demux_16_5be8a8cb_1 (
    .in_2(Write_Select_t[2:0]), .Y(controlled_buffer_4_out), .L_2_9682dceb({Write_D, Write_DE_Pair}),
    .L_3_c2e8e44e(Write_Stack), .L_4_5ba2c680({Write_H, Write_HL_Pair}),
    .L_0_5ac68a80({Write_B, Write_BC_Pair}), .L_5_c7845d74(Addr_Load),
    .L_6_a1ac0909({Write_W, Write_WZ_Pair}), .L_1_ab49ad53(Write_PC));  // open: L_7_4b7fadd1
  assign Write_Select_t = ~Write_Select;  // NOT_Gate not_4, 4 bits wide
  assign {not_5_out_2[3], not_5_out} = ~Bus_Read_Write;  // NOT_Gate not_5, 4 bits wide
  assign controlled_buffer_5_out = not_5_out_2[3] ? Bus_In : 8'bz;  // Controlled_Buffer controlled_buffer_5
  L_8_1_Demux_8_58d4daa4 l_8_1_demux_8_58d4daa4_2 (
    .in_2(not_5_out), .Y(controlled_buffer_5_out), .L_2_9682dceb(Write_D), .L_3_c2e8e44e(Write_DE_Pair),
    .L_4_5ba2c680(Write_H), .L_0_5ac68a80(Write_B), .L_5_c7845d74(Write_HL_Pair), .L_6_a1ac0909(Write_W),
    .L_7_4b7fadd1(Write_WZ_Pair), .L_1_ab49ad53(Write_BC_Pair));
  Register_8_252a90b2 Tmp_W (.In(Write_W), .W(1'b1), .Clk(Clock), .Out(Read_WZ_Pair[15:8]));  // open: Clear
  Register_8_252a90b2 Reg_B (.In(Write_B), .W(1'b1), .Clk(Clock), .Out(B));  // open: Clear
  Register_8_252a90b2 Reg_D (.In(Write_D), .W(1'b1), .Clk(Clock), .Out(D));  // open: Clear
  Register_8_252a90b2 Reg_H (.In(Write_H), .W(1'b1), .Clk(Clock), .Out(H));  // open: Clear
  assign Bus_Out = not_6_out ? mux_8_2_out_10 : 8'bz;  // Controlled_Buffer controlled_buffer_6
  not not_6 (not_6_out, not_5_out_2[3]);
  Mux_8 mux_8_2 (
    .in_9(not_5_out), .p4(H), .p5(L), .p6(Read_WZ_Pair[15:8]), .p7(Read_WZ_Pair[7:0]), .p0(B), .p1(C),
    .p2(D), .p3(E), .out_10(mux_8_2_out_10));
  assign Write_16 = z_detector_1_be9a67f0_1_out_2 ? Read_16 : 16'bz;  // Controlled_Buffer controlled_buffer_7
  Register_8_252a90b2 Tmp_Z (.In(Write_WZ_Pair), .W(1'b1), .Clk(Clock), .Out(Read_WZ_Pair[7:0]));  // open: Clear
  Register_8_252a90b2 Reg_C (.In(Write_BC_Pair), .W(1'b1), .Clk(Clock), .Out(C));  // open: Clear
  Register_8_252a90b2 Reg_E (.In(Write_DE_Pair), .W(1'b1), .Clk(Clock), .Out(E));  // open: Clear
  Register_8_252a90b2 Reg_L (.In(Write_HL_Pair), .W(1'b1), .Clk(Clock), .Out(L));  // open: Clear
  Z_Detector_1_be9a67f0 z_detector_1_be9a67f0_1 (.in_1(Increment_Decrement), .out_2(z_detector_1_be9a67f0_1_out_2));
  assign Write_8 = z_detector_1_be9a67f0_1_out_2 ? Read_8 : 8'bz;  // Controlled_Buffer controlled_buffer_8
  Register_16_2fb72861 register_16_2fb72861_2 (.W(1'b1), .In(Write_Stack), .Clk(Clock), .Out(Stack));  // open: Clear
  Register_16_2fb72861 register_16_2fb72861_3 (.W(1'b1), .In(Write_PC), .Clk(Clock), .Out(PC));  // open: Clear
  Inc_dec_16_1df549c4 inc_dec_16_1df549c4_1 (
    .In(Read_16), .Inc_Dec_32c9cf86(Increment_Decrement), .Carry_Barrow_In_ee85c3ba(not_7_out),
    .Out(inc_dec_16_1df549c4_1_out));  // open: Carry_Barrow_Out_8faccd5f
  assign Write_16 = not_7_out ? inc_dec_16_1df549c4_1_out : 16'bz;  // Controlled_Buffer controlled_buffer_9
  Error_Detector_16_c93c636a error_detector_16_c93c636a_1 (.In(z_detector_16_47ed8cfc_1_out_2), .Out({Error, Error}));
  Z_Detector_16_47ed8cfc z_detector_16_47ed8cfc_1 (.in_1(PC), .out_2(z_detector_16_47ed8cfc_1_out_2));
  Z_Detector_16_47ed8cfc z_detector_16_47ed8cfc_2 (.in_1(Mem_Bus), .out_2(z_detector_16_47ed8cfc_1_out_2));
  Z_Detector_16_47ed8cfc z_detector_16_47ed8cfc_3 (.in_1(Stack), .out_2(z_detector_16_47ed8cfc_1_out_2));
  Z_Detector_8_e7b9c500 z_detector_8_e7b9c500_1 (.in_1(B), .out_2(Error));
  Z_Detector_8_e7b9c500 z_detector_8_e7b9c500_2 (.in_1(D), .out_2(Error));
  Z_Detector_1_be9a67f0 z_detector_1_be9a67f0_2 (.in_1(Increment_Decrement), .out_2(z_detector_1_be9a67f0_2_out_2));
  not not_7 (not_7_out, z_detector_1_be9a67f0_2_out_2);
  Inc_dec_8_1e64ec11 inc_dec_8_1e64ec11_1 (
    .In(Read_8), .Inc_Dec_32c9cf86(Increment_Decrement), .Carry_Barrow_In_ee85c3ba(not_7_out),
    .Out(inc_dec_8_1e64ec11_1_out));  // open: Carry_Barrow_Out_8faccd5f
  Controlled_Buffer #(.width(8)) controlled_buffer_10 (.in(inc_dec_8_1e64ec11_1_out), .en(not_7_out));  // open: out
  Z_Detector_8_e7b9c500 z_detector_8_e7b9c500_3 (.in_1(H), .out_2(Error));
  Z_Detector_8_e7b9c500 z_detector_8_e7b9c500_4 (.in_1(Read_WZ_Pair[15:8]), .out_2(Error));
  Z_Detector_8_e7b9c500 z_detector_8_e7b9c500_5 (.in_1(C), .out_2(Error));
  Z_Detector_8_e7b9c500 z_detector_8_e7b9c500_6 (.in_1(E), .out_2(Error));
  Z_Detector_8_e7b9c500 z_detector_8_e7b9c500_7 (.in_1(L), .out_2(Error));
  Z_Detector_8_e7b9c500 z_detector_8_e7b9c500_8 (.in_1(Read_WZ_Pair[7:0]), .out_2(Error));

  // Other names for the same wires on the sheet: Addr_Read[15:0] = Mem_Bus; I_D = Increment_Decrement;
  //   Read_BC_Pair[15:0] = {B, C}; Read_DE_Pair[15:0] = {D, E}; Read_HL_Pair[15:0] = {H, L};
  //   Z[7:0] = Read_WZ_Pair[7:0]; W[7:0] = Read_WZ_Pair[15:8]; Write_C[7:0] = Write_BC_Pair;
  //   Write_BC_Pair[15:8] = Write_B; Write_E[7:0] = Write_DE_Pair; Write_DE_Pair[15:8] = Write_D;
  //   Write_L[7:0] = Write_HL_Pair; Write_HL_Pair[15:8] = Write_H; Write_Z[7:0] = Write_WZ_Pair;
  //   Write_WZ_Pair[15:8] = Write_W

  // Notes on the sheet:
  //   Read_Select: pull=down
  //   Write_Select: pull=down
  //   Bus_Read_Write: pull=down
  //   Pairs can only map to other 16 bit pairs/registers
  //   Moves read to write if not incrementing/decrementing
endmodule
