// Logisim project Timing Phase.circ as structural Verilog: 1 circuit, main circuit Phase_Timer_08e5fbac
module Phase_Timer_08e5fbac (
  input  Phase_1_594ebbd0,
  input  Phase_2_e5f6d7db
);

  Clock clock_1 ();  // open: out
endmodule
