// Logisim project Timing and Control.circ as structural Verilog: 1 circuit, main circuit Timing_and_Control_69b40432
module Timing_and_Control_69b40432 (
  input  Reset,
  input  in_2,
  input  Hold,
  input  Ready,
  input  Ph1,
  input  Ph2,
  input  En,
  output [2:0] En_Left_c4fceaa9,
  output [5:0] En_Right_4b6c2cb1,
  output Clk,
  output [7:0] Registry_Control_d1edc509,
  output [3:0] ALU_Control_caaca333,
  output L_WR_581d48aa,
  output DBIN,
  output INTE,
  output Hold_Ack_9e453571,
  output Wait,
  output Sync
);


  assign ALU_Control_caaca333 = 4'b0000;
  assign Clk = 1'b0;
  assign DBIN = 1'b0;
  assign En_Left_c4fceaa9 = 3'b000;
  assign En_Right_4b6c2cb1 = {6{1'b0}};
  assign Hold_Ack_9e453571 = 1'b0;
  assign INTE = 1'b0;
  assign L_WR_581d48aa = 1'b0;
  assign Registry_Control_d1edc509 = {8{1'b0}};
  assign Sync = 1'b0;
  assign Wait = 1'b0;

  // Notes on the sheet:
  //   En: pull=down
  //   En_Right_4b6c2cb1: pull=down
  //   En_Left_c4fceaa9: pull=down
endmodule
