// Logisim project counter.circ as structural Verilog: 5 circuits, main circuit Counter_16_88db71ed
module Counter_16_88db71ed (
  input  Clk,
  input  En,
  input  Clear,
  output [15:0] Count
);

  wire and_1_out, and_2_out, and_3_out, and_4_out, and_5_out, and_6_out, and_7_out, and_8_out, and_9_out,
       and_10_out, and_11_out, and_12_out, and_13_out, and_14_out;

  JK_Flip_Flop_0cb27562 jk_flip_flop_0cb27562_1 (
    .J(1'b1), .K(1'b1), .Clear(Clear), .En(En), .Clock(Clk), .Output(Count[0]));
  JK_Flip_Flop_0cb27562 jk_flip_flop_0cb27562_2 (
    .J(Count[0]), .K(Count[0]), .Clear(Clear), .En(En), .Clock(Clk), .Output(Count[1]));
  and and_1 (and_1_out, Count[0], Count[1]);
  JK_Flip_Flop_0cb27562 jk_flip_flop_0cb27562_3 (
    .J(and_1_out), .K(and_1_out), .Clear(Clear), .En(En), .Clock(Clk), .Output(Count[2]));
  and and_2 (and_2_out, and_1_out, Count[2]);
  JK_Flip_Flop_0cb27562 jk_flip_flop_0cb27562_4 (
    .J(and_2_out), .K(and_2_out), .Clear(Clear), .En(En), .Clock(Clk), .Output(Count[3]));
  and and_3 (and_3_out, and_2_out, Count[3]);
  JK_Flip_Flop_0cb27562 jk_flip_flop_0cb27562_5 (
    .J(and_3_out), .K(and_3_out), .Clear(Clear), .En(En), .Clock(Clk), .Output(Count[4]));
  and and_4 (and_4_out, and_3_out, Count[4]);
  JK_Flip_Flop_0cb27562 jk_flip_flop_0cb27562_6 (
    .J(and_4_out), .K(and_4_out), .Clear(Clear), .En(En), .Clock(Clk), .Output(Count[5]));
  and and_5 (and_5_out, and_4_out, Count[5]);
  JK_Flip_Flop_0cb27562 jk_flip_flop_0cb27562_7 (
    .J(and_5_out), .K(and_5_out), .Clear(Clear), .En(En), .Clock(Clk), .Output(Count[6]));
  and and_6 (and_6_out, and_5_out, Count[6]);
  JK_Flip_Flop_0cb27562 jk_flip_flop_0cb27562_8 (
    .J(and_6_out), .K(and_6_out), .Clear(Clear), .En(En), .Clock(Clk), .Output(Count[7]));
  and and_7 (and_7_out, and_6_out, Count[7]);
  JK_Flip_Flop_0cb27562 jk_flip_flop_0cb27562_9 (
    .J(and_7_out), .K(and_7_out), .Clear(Clear), .En(En), .Clock(Clk), .Output(Count[8]));
  and and_8 (and_8_out, and_7_out, Count[8]);
  JK_Flip_Flop_0cb27562 jk_flip_flop_0cb27562_10 (
    .J(and_8_out), .K(and_8_out), .Clear(Clear), .En(En), .Clock(Clk), .Output(Count[9]));
  and and_9 (and_9_out, and_8_out, Count[9]);
  JK_Flip_Flop_0cb27562 jk_flip_flop_0cb27562_11 (
    .J(and_9_out), .K(and_9_out), .Clear(Clear), .En(En), .Clock(Clk), .Output(Count[10]));
  and and_10 (and_10_out, and_9_out, Count[10]);
  JK_Flip_Flop_0cb27562 jk_flip_flop_0cb27562_12 (
    .J(and_10_out), .K(and_10_out), .Clear(Clear), .En(En), .Clock(Clk), .Output(Count[11]));
  and and_11 (and_11_out, and_10_out, Count[11]);
  JK_Flip_Flop_0cb27562 jk_flip_flop_0cb27562_13 (
    .J(and_11_out), .K(and_11_out), .Clear(Clear), .En(En), .Clock(Clk), .Output(Count[12]));
  and and_12 (and_12_out, and_11_out, Count[12]);
  JK_Flip_Flop_0cb27562 jk_flip_flop_0cb27562_14 (
    .J(and_12_out), .K(and_12_out), .Clear(Clear), .En(En), .Clock(Clk), .Output(Count[13]));
  and and_13 (and_13_out, and_12_out, Count[13]);
  JK_Flip_Flop_0cb27562 jk_flip_flop_0cb27562_15 (
    .J(and_13_out), .K(and_13_out), .Clear(Clear), .En(En), .Clock(Clk), .Output(Count[14]));
  and and_14 (and_14_out, and_13_out, Count[14]);
  JK_Flip_Flop_0cb27562 jk_flip_flop_0cb27562_16 (
    .J(and_14_out), .K(and_14_out), .Clear(Clear), .En(En), .Clock(Clk), .Output(Count[15]));

  // Notes on the sheet:
  //   Clear: pull=down
  //   En: pull=down
endmodule

module Counter_8_b01f752f (
  input  Clk,
  input  En,
  input  Clear,
  output [7:0] Count
);

  wire and_1_out, and_2_out, and_3_out, and_4_out, and_5_out, and_6_out;

  JK_Flip_Flop_0cb27562 jk_flip_flop_0cb27562_1 (
    .J(1'b1), .K(1'b1), .Clear(Clear), .En(En), .Clock(Clk), .Output(Count[0]));
  JK_Flip_Flop_0cb27562 jk_flip_flop_0cb27562_2 (
    .J(Count[0]), .K(Count[0]), .Clear(Clear), .En(En), .Clock(Clk), .Output(Count[1]));
  and and_1 (and_1_out, Count[0], Count[1]);
  JK_Flip_Flop_0cb27562 jk_flip_flop_0cb27562_3 (
    .J(and_1_out), .K(and_1_out), .Clear(Clear), .En(En), .Clock(Clk), .Output(Count[2]));
  and and_2 (and_2_out, and_1_out, Count[2]);
  JK_Flip_Flop_0cb27562 jk_flip_flop_0cb27562_4 (
    .J(and_2_out), .K(and_2_out), .Clear(Clear), .En(En), .Clock(Clk), .Output(Count[3]));
  and and_3 (and_3_out, and_2_out, Count[3]);
  JK_Flip_Flop_0cb27562 jk_flip_flop_0cb27562_5 (
    .J(and_3_out), .K(and_3_out), .Clear(Clear), .En(En), .Clock(Clk), .Output(Count[4]));
  and and_4 (and_4_out, and_3_out, Count[4]);
  JK_Flip_Flop_0cb27562 jk_flip_flop_0cb27562_6 (
    .J(and_4_out), .K(and_4_out), .Clear(Clear), .En(En), .Clock(Clk), .Output(Count[5]));
  and and_5 (and_5_out, and_4_out, Count[5]);
  JK_Flip_Flop_0cb27562 jk_flip_flop_0cb27562_7 (
    .J(and_5_out), .K(and_5_out), .Clear(Clear), .En(En), .Clock(Clk), .Output(Count[6]));
  and and_6 (and_6_out, and_5_out, Count[6]);
  JK_Flip_Flop_0cb27562 jk_flip_flop_0cb27562_8 (
    .J(and_6_out), .K(and_6_out), .Clear(Clear), .En(En), .Clock(Clk), .Output(Count[7]));

  // Notes on the sheet:
  //   En: pull=down
  //   Clear: pull=down
endmodule

module Counter_4_be7a77e1 (
  input  Clk,
  input  En,
  input  Clear,
  output [7:0] Count
);

  wire and_1_out, and_2_out, and_3_out, and_4_out, and_5_out, and_6_out;

  JK_Flip_Flop_0cb27562 jk_flip_flop_0cb27562_1 (
    .J(1'b1), .K(1'b1), .Clear(Clear), .En(En), .Clock(Clk), .Output(Count[0]));
  JK_Flip_Flop_0cb27562 jk_flip_flop_0cb27562_2 (
    .J(Count[0]), .K(Count[0]), .Clear(Clear), .En(En), .Clock(Clk), .Output(Count[1]));
  and and_1 (and_1_out, Count[0], Count[1]);
  JK_Flip_Flop_0cb27562 jk_flip_flop_0cb27562_3 (
    .J(and_1_out), .K(and_1_out), .Clear(Clear), .En(En), .Clock(Clk), .Output(Count[2]));
  and and_2 (and_2_out, and_1_out, Count[2]);
  JK_Flip_Flop_0cb27562 jk_flip_flop_0cb27562_4 (
    .J(and_2_out), .K(and_2_out), .Clear(Clear), .En(En), .Clock(Clk), .Output(Count[3]));
  and and_3 (and_3_out, and_2_out, Count[3]);
  JK_Flip_Flop_0cb27562 jk_flip_flop_0cb27562_5 (
    .J(and_3_out), .K(and_3_out), .Clear(Clear), .En(En), .Clock(Clk), .Output(Count[4]));
  and and_4 (and_4_out, and_3_out, Count[4]);
  JK_Flip_Flop_0cb27562 jk_flip_flop_0cb27562_6 (
    .J(and_4_out), .K(and_4_out), .Clear(Clear), .En(En), .Clock(Clk), .Output(Count[5]));
  and and_5 (and_5_out, and_4_out, Count[5]);
  JK_Flip_Flop_0cb27562 jk_flip_flop_0cb27562_7 (
    .J(and_5_out), .K(and_5_out), .Clear(Clear), .En(En), .Clock(Clk), .Output(Count[6]));
  and and_6 (and_6_out, and_5_out, Count[6]);
  JK_Flip_Flop_0cb27562 jk_flip_flop_0cb27562_8 (
    .J(and_6_out), .K(and_6_out), .Clear(Clear), .En(En), .Clock(Clk), .Output(Count[7]));

  // Notes on the sheet:
  //   En: pull=down
  //   Clear: pull=down
endmodule

module Counter_2_15e20b60 (
  input  Clk,
  input  En,
  input  Clear,
  output [1:0] Count
);

  JK_Flip_Flop_0cb27562 jk_flip_flop_0cb27562_1 (
    .J(1'b1), .K(1'b1), .Clear(Clear), .En(En), .Clock(Clk), .Output(Count[1]));
  JK_Flip_Flop_0cb27562 jk_flip_flop_0cb27562_2 (
    .J(Count[1]), .K(Count[1]), .Clear(Clear), .En(En), .Clock(Clk), .Output(Count[0]));

  // Notes on the sheet:
  //   En: pull=down
  //   Clear: pull=down
endmodule

module Counter_1_ddfe57c6 (
  input  Clk,
  input  En,
  input  Clear,
  output Count
);

  JK_Flip_Flop_0cb27562 jk_flip_flop_0cb27562_1 (
    .J(1'b1), .K(1'b1), .Clear(Clear), .En(En), .Clock(Clk), .Output(Count));

  // Notes on the sheet:
  //   En: pull=down
  //   Clear: pull=down
endmodule
