// Logisim project 2-1 Demux.circ as structural Verilog: 5 circuits, main circuit L_2_1_Demux_16_b3f74e14
module L_2_1_Demux_16_b3f74e14 (
  input  [15:0] Y,
  input  Select,
  output [15:0] L_0_f163cde3,
  output [15:0] L_1_507cfd33
);

  wire not_1_out;

  assign L_0_f163cde3 = not_1_out ? Y : 16'bz;  // Controlled_Buffer controlled_buffer_1
  not not_1 (not_1_out, Select);
  assign L_1_507cfd33 = Select ? Y : 16'bz;  // Controlled_Buffer controlled_buffer_2
endmodule

module L_2_1_Demux_8_2e02d5b2 (
  input  [7:0] Y,
  input  Select,
  output [7:0] L_0_f163cde3,
  output [7:0] L_1_507cfd33
);

  wire not_1_out;

  assign L_0_f163cde3 = not_1_out ? Y : 8'bz;  // Controlled_Buffer controlled_buffer_1
  not not_1 (not_1_out, Select);
  assign L_1_507cfd33 = Select ? Y : 8'bz;  // Controlled_Buffer controlled_buffer_2
endmodule

module L_2_1_Demux_4_3f3c28b6 (
  input  [3:0] Y,
  input  Select,
  output [3:0] L_0_f163cde3,
  output [3:0] L_1_507cfd33
);

  wire not_1_out;

  assign L_0_f163cde3 = not_1_out ? Y : 4'bz;  // Controlled_Buffer controlled_buffer_1
  not not_1 (not_1_out, Select);
  assign L_1_507cfd33 = Select ? Y : 4'bz;  // Controlled_Buffer controlled_buffer_2
endmodule

module L_2_1_Demux_2_124803d2 (
  input  [1:0] Y,
  input  Select,
  output [1:0] L_0_f163cde3,
  output [1:0] L_1_507cfd33
);

  wire not_1_out;

  assign L_0_f163cde3 = not_1_out ? Y : 2'bz;  // Controlled_Buffer controlled_buffer_1
  not not_1 (not_1_out, Select);
  assign L_1_507cfd33 = Select ? Y : 2'bz;  // Controlled_Buffer controlled_buffer_2
endmodule

module L_2_1_Demux_1_138d94c5 (
  input  Y,
  input  Select,
  output L_0_f163cde3,
  output L_1_507cfd33
);

  wire not_1_out;

  assign L_0_f163cde3 = not_1_out ? Y : 1'bz;  // Controlled_Buffer controlled_buffer_1
  not not_1 (not_1_out, Select);
  assign L_1_507cfd33 = Select ? Y : 1'bz;  // Controlled_Buffer controlled_buffer_2
endmodule
