// Logisim project 4-1 Demux.circ as structural Verilog: 5 circuits, main circuit L_4_1_Demux_16_83ae0d9a
module L_4_1_Demux_16_83ae0d9a (
  input  [15:0] Y,
  input  [1:0] Select,
  output [15:0] L_0_6365c324,
  output [15:0] L_1_bd4f4f3d,
  output [15:0] L_2_061b0e56,
  output [15:0] L_3_85f728ad
);

  wire l_2_4_decoder_162577e0_1_l_0_71f7447a, l_2_4_decoder_162577e0_1_l_1_2e59f046,
       l_2_4_decoder_162577e0_1_l_2_6856bdbb, l_2_4_decoder_162577e0_1_l_3_5fdef051;

  L_2_4_Decoder_162577e0 l_2_4_decoder_162577e0_1 (
    .En(1'b1), .Select(Select), .L_2_6856bdbb(l_2_4_decoder_162577e0_1_l_2_6856bdbb),
    .L_3_5fdef051(l_2_4_decoder_162577e0_1_l_3_5fdef051),
    .L_0_71f7447a(l_2_4_decoder_162577e0_1_l_0_71f7447a), .L_1_2e59f046(l_2_4_decoder_162577e0_1_l_1_2e59f046));
  assign L_0_6365c324 = l_2_4_decoder_162577e0_1_l_0_71f7447a ? Y : 16'bz;  // Controlled_Buffer controlled_buffer_1
  assign L_1_bd4f4f3d = l_2_4_decoder_162577e0_1_l_1_2e59f046 ? Y : 16'bz;  // Controlled_Buffer controlled_buffer_2
  assign L_2_061b0e56 = l_2_4_decoder_162577e0_1_l_2_6856bdbb ? Y : 16'bz;  // Controlled_Buffer controlled_buffer_3
  assign L_3_85f728ad = l_2_4_decoder_162577e0_1_l_3_5fdef051 ? Y : 16'bz;  // Controlled_Buffer controlled_buffer_4
endmodule

module L_4_1_Demux_8_4e72f2d4 (
  input  [7:0] Y,
  input  [1:0] Select,
  output [7:0] L_0_6365c324,
  output [7:0] L_1_bd4f4f3d,
  output [7:0] L_2_061b0e56,
  output [7:0] L_3_85f728ad
);

  wire l_2_4_decoder_162577e0_1_l_0_71f7447a, l_2_4_decoder_162577e0_1_l_1_2e59f046,
       l_2_4_decoder_162577e0_1_l_2_6856bdbb, l_2_4_decoder_162577e0_1_l_3_5fdef051;

  L_2_4_Decoder_162577e0 l_2_4_decoder_162577e0_1 (
    .En(1'b1), .Select(Select), .L_2_6856bdbb(l_2_4_decoder_162577e0_1_l_2_6856bdbb),
    .L_3_5fdef051(l_2_4_decoder_162577e0_1_l_3_5fdef051),
    .L_0_71f7447a(l_2_4_decoder_162577e0_1_l_0_71f7447a), .L_1_2e59f046(l_2_4_decoder_162577e0_1_l_1_2e59f046));
  assign L_0_6365c324 = l_2_4_decoder_162577e0_1_l_0_71f7447a ? Y : 8'bz;  // Controlled_Buffer controlled_buffer_1
  assign L_1_bd4f4f3d = l_2_4_decoder_162577e0_1_l_1_2e59f046 ? Y : 8'bz;  // Controlled_Buffer controlled_buffer_2
  assign L_2_061b0e56 = l_2_4_decoder_162577e0_1_l_2_6856bdbb ? Y : 8'bz;  // Controlled_Buffer controlled_buffer_3
  assign L_3_85f728ad = l_2_4_decoder_162577e0_1_l_3_5fdef051 ? Y : 8'bz;  // Controlled_Buffer controlled_buffer_4
endmodule

module L_4_1_Demux_4_b877160d (
  input  [3:0] Y,
  input  [1:0] Select,
  output [3:0] L_0_6365c324,
  output [3:0] L_1_bd4f4f3d,
  output [3:0] L_2_061b0e56,
  output [3:0] L_3_85f728ad
);

  wire l_2_4_decoder_162577e0_1_l_0_71f7447a, l_2_4_decoder_162577e0_1_l_1_2e59f046,
       l_2_4_decoder_162577e0_1_l_2_6856bdbb, l_2_4_decoder_162577e0_1_l_3_5fdef051;

  L_2_4_Decoder_162577e0 l_2_4_decoder_162577e0_1 (
    .En(1'b1), .Select(Select), .L_2_6856bdbb(l_2_4_decoder_162577e0_1_l_2_6856bdbb),
    .L_3_5fdef051(l_2_4_decoder_162577e0_1_l_3_5fdef051),
    .L_0_71f7447a(l_2_4_decoder_162577e0_1_l_0_71f7447a), .L_1_2e59f046(l_2_4_decoder_162577e0_1_l_1_2e59f046));
  assign L_0_6365c324 = l_2_4_decoder_162577e0_1_l_0_71f7447a ? Y : 4'bz;  // Controlled_Buffer controlled_buffer_1
  assign L_1_bd4f4f3d = l_2_4_decoder_162577e0_1_l_1_2e59f046 ? Y : 4'bz;  // Controlled_Buffer controlled_buffer_2
  assign L_2_061b0e56 = l_2_4_decoder_162577e0_1_l_2_6856bdbb ? Y : 4'bz;  // Controlled_Buffer controlled_buffer_3
  assign L_3_85f728ad = l_2_4_decoder_162577e0_1_l_3_5fdef051 ? Y : 4'bz;  // Controlled_Buffer controlled_buffer_4
endmodule

module L_4_1_Demux_2_b0bbb9cc (
  input  [1:0] Y,
  input  [1:0] Select,
  output [1:0] L_0_6365c324,
  output [1:0] L_1_bd4f4f3d,
  output [1:0] L_2_061b0e56,
  output [1:0] L_3_85f728ad
);

  wire l_2_4_decoder_162577e0_1_l_0_71f7447a, l_2_4_decoder_162577e0_1_l_1_2e59f046,
       l_2_4_decoder_162577e0_1_l_2_6856bdbb, l_2_4_decoder_162577e0_1_l_3_5fdef051;

  L_2_4_Decoder_162577e0 l_2_4_decoder_162577e0_1 (
    .En(1'b1), .Select(Select), .L_2_6856bdbb(l_2_4_decoder_162577e0_1_l_2_6856bdbb),
    .L_3_5fdef051(l_2_4_decoder_162577e0_1_l_3_5fdef051),
    .L_0_71f7447a(l_2_4_decoder_162577e0_1_l_0_71f7447a), .L_1_2e59f046(l_2_4_decoder_162577e0_1_l_1_2e59f046));
  assign L_0_6365c324 = l_2_4_decoder_162577e0_1_l_0_71f7447a ? Y : 2'bz;  // Controlled_Buffer controlled_buffer_1
  assign L_1_bd4f4f3d = l_2_4_decoder_162577e0_1_l_1_2e59f046 ? Y : 2'bz;  // Controlled_Buffer controlled_buffer_2
  assign L_2_061b0e56 = l_2_4_decoder_162577e0_1_l_2_6856bdbb ? Y : 2'bz;  // Controlled_Buffer controlled_buffer_3
  assign L_3_85f728ad = l_2_4_decoder_162577e0_1_l_3_5fdef051 ? Y : 2'bz;  // Controlled_Buffer controlled_buffer_4
endmodule

module L_4_1_Demux_1_7dcd588f (
  input  Y,
  input  [1:0] Select,
  output L_0_6365c324,
  output L_1_bd4f4f3d,
  output L_2_061b0e56,
  output L_3_85f728ad
);

  wire l_2_4_decoder_162577e0_1_l_0_71f7447a, l_2_4_decoder_162577e0_1_l_1_2e59f046,
       l_2_4_decoder_162577e0_1_l_2_6856bdbb, l_2_4_decoder_162577e0_1_l_3_5fdef051;

  L_2_4_Decoder_162577e0 l_2_4_decoder_162577e0_1 (
    .En(1'b1), .Select(Select), .L_2_6856bdbb(l_2_4_decoder_162577e0_1_l_2_6856bdbb),
    .L_3_5fdef051(l_2_4_decoder_162577e0_1_l_3_5fdef051),
    .L_0_71f7447a(l_2_4_decoder_162577e0_1_l_0_71f7447a), .L_1_2e59f046(l_2_4_decoder_162577e0_1_l_1_2e59f046));
  assign L_0_6365c324 = l_2_4_decoder_162577e0_1_l_0_71f7447a ? Y : 1'bz;  // Controlled_Buffer controlled_buffer_1
  assign L_1_bd4f4f3d = l_2_4_decoder_162577e0_1_l_1_2e59f046 ? Y : 1'bz;  // Controlled_Buffer controlled_buffer_2
  assign L_2_061b0e56 = l_2_4_decoder_162577e0_1_l_2_6856bdbb ? Y : 1'bz;  // Controlled_Buffer controlled_buffer_3
  assign L_3_85f728ad = l_2_4_decoder_162577e0_1_l_3_5fdef051 ? Y : 1'bz;  // Controlled_Buffer controlled_buffer_4
endmodule
