// Logisim project 8-1 Demux.circ as structural Verilog: 5 circuits, main circuit L_8_1_Demux_16_5be8a8cb
module L_8_1_Demux_16_5be8a8cb (
  input  [15:0] Y,
  input  [2:0] in_2,
  output [15:0] L_0_5ac68a80,
  output [15:0] L_1_ab49ad53,
  output [15:0] L_2_9682dceb,
  output [15:0] L_3_c2e8e44e,
  output [15:0] L_4_5ba2c680,
  output [15:0] L_5_c7845d74,
  output [15:0] L_6_a1ac0909,
  output [15:0] L_7_4b7fadd1
);

  wire [15:0] l_2_1_demux_16_b3f74e14_1_l_0_f163cde3, l_2_1_demux_16_b3f74e14_1_l_1_507cfd33;

  L_2_1_Demux_16_b3f74e14 l_2_1_demux_16_b3f74e14_1 (
    .Select(in_2[2]), .Y(Y), .L_0_f163cde3(l_2_1_demux_16_b3f74e14_1_l_0_f163cde3),
    .L_1_507cfd33(l_2_1_demux_16_b3f74e14_1_l_1_507cfd33));
  L_4_1_Demux_16_83ae0d9a l_4_1_demux_16_83ae0d9a_1 (
    .Select(in_2[1:0]), .Y(l_2_1_demux_16_b3f74e14_1_l_0_f163cde3), .L_1_bd4f4f3d(L_1_ab49ad53),
    .L_2_061b0e56(L_2_9682dceb), .L_3_85f728ad(L_3_c2e8e44e), .L_0_6365c324(L_0_5ac68a80));
  L_4_1_Demux_16_83ae0d9a l_4_1_demux_16_83ae0d9a_2 (
    .Select(in_2[1:0]), .Y(l_2_1_demux_16_b3f74e14_1_l_1_507cfd33), .L_1_bd4f4f3d(L_5_c7845d74),
    .L_2_061b0e56(L_6_a1ac0909), .L_3_85f728ad(L_7_4b7fadd1), .L_0_6365c324(L_4_5ba2c680));
endmodule

module L_8_1_Demux_8_58d4daa4 (
  input  [7:0] Y,
  input  [2:0] in_2,
  output [7:0] L_0_5ac68a80,
  output [7:0] L_1_ab49ad53,
  output [7:0] L_2_9682dceb,
  output [7:0] L_3_c2e8e44e,
  output [7:0] L_4_5ba2c680,
  output [7:0] L_5_c7845d74,
  output [7:0] L_6_a1ac0909,
  output [7:0] L_7_4b7fadd1
);

  wire [7:0] l_2_1_demux_8_2e02d5b2_1_l_0_f163cde3, l_2_1_demux_8_2e02d5b2_1_l_1_507cfd33;

  L_2_1_Demux_8_2e02d5b2 l_2_1_demux_8_2e02d5b2_1 (
    .Select(in_2[2]), .Y(Y), .L_0_f163cde3(l_2_1_demux_8_2e02d5b2_1_l_0_f163cde3),
    .L_1_507cfd33(l_2_1_demux_8_2e02d5b2_1_l_1_507cfd33));
  L_4_1_Demux_8_4e72f2d4 l_4_1_demux_8_4e72f2d4_1 (
    .Select(in_2[1:0]), .Y(l_2_1_demux_8_2e02d5b2_1_l_0_f163cde3), .L_1_bd4f4f3d(L_1_ab49ad53),
    .L_2_061b0e56(L_2_9682dceb), .L_3_85f728ad(L_3_c2e8e44e), .L_0_6365c324(L_0_5ac68a80));
  L_4_1_Demux_8_4e72f2d4 l_4_1_demux_8_4e72f2d4_2 (
    .Select(in_2[1:0]), .Y(l_2_1_demux_8_2e02d5b2_1_l_1_507cfd33), .L_1_bd4f4f3d(L_5_c7845d74),
    .L_2_061b0e56(L_6_a1ac0909), .L_3_85f728ad(L_7_4b7fadd1), .L_0_6365c324(L_4_5ba2c680));
endmodule

module L_8_1_Demux_4_3b2db8e2 (
  input  [3:0] Y,
  input  [2:0] in_2,
  output [3:0] L_0_5ac68a80,
  output [3:0] L_1_ab49ad53,
  output [3:0] L_2_9682dceb,
  output [3:0] L_3_c2e8e44e,
  output [3:0] L_4_5ba2c680,
  output [3:0] L_5_c7845d74,
  output [3:0] L_6_a1ac0909,
  output [3:0] L_7_4b7fadd1
);

  wire [3:0] l_2_1_demux_4_3f3c28b6_1_l_0_f163cde3, l_2_1_demux_4_3f3c28b6_1_l_1_507cfd33;

  L_2_1_Demux_4_3f3c28b6 l_2_1_demux_4_3f3c28b6_1 (
    .Select(in_2[2]), .Y(Y), .L_0_f163cde3(l_2_1_demux_4_3f3c28b6_1_l_0_f163cde3),
    .L_1_507cfd33(l_2_1_demux_4_3f3c28b6_1_l_1_507cfd33));
  L_4_1_Demux_4_b877160d l_4_1_demux_4_b877160d_1 (
    .Select(in_2[1:0]), .Y(l_2_1_demux_4_3f3c28b6_1_l_0_f163cde3), .L_1_bd4f4f3d(L_1_ab49ad53),
    .L_2_061b0e56(L_2_9682dceb), .L_3_85f728ad(L_3_c2e8e44e), .L_0_6365c324(L_0_5ac68a80));
  L_4_1_Demux_4_b877160d l_4_1_demux_4_b877160d_2 (
    .Select(in_2[1:0]), .Y(l_2_1_demux_4_3f3c28b6_1_l_1_507cfd33), .L_1_bd4f4f3d(L_5_c7845d74),
    .L_2_061b0e56(L_6_a1ac0909), .L_3_85f728ad(L_7_4b7fadd1), .L_0_6365c324(L_4_5ba2c680));
endmodule

module L_8_1_Demux_2_74c68883 (
  input  [1:0] Y,
  input  [2:0] in_2,
  output [1:0] L_0_5ac68a80,
  output [1:0] L_1_ab49ad53,
  output [1:0] L_2_9682dceb,
  output [1:0] L_3_c2e8e44e,
  output [1:0] L_4_5ba2c680,
  output [1:0] L_5_c7845d74,
  output [1:0] L_6_a1ac0909,
  output [1:0] L_7_4b7fadd1
);

  wire [1:0] l_2_1_demux_2_124803d2_1_l_0_f163cde3, l_2_1_demux_2_124803d2_1_l_1_507cfd33;

  L_2_1_Demux_2_124803d2 l_2_1_demux_2_124803d2_1 (
    .Select(in_2[2]), .Y(Y), .L_0_f163cde3(l_2_1_demux_2_124803d2_1_l_0_f163cde3),
    .L_1_507cfd33(l_2_1_demux_2_124803d2_1_l_1_507cfd33));
  L_4_1_Demux_2_b0bbb9cc l_4_1_demux_2_b0bbb9cc_1 (
    .Select(in_2[1:0]), .Y(l_2_1_demux_2_124803d2_1_l_0_f163cde3), .L_1_bd4f4f3d(L_1_ab49ad53),
    .L_2_061b0e56(L_2_9682dceb), .L_3_85f728ad(L_3_c2e8e44e), .L_0_6365c324(L_0_5ac68a80));
  L_4_1_Demux_2_b0bbb9cc l_4_1_demux_2_b0bbb9cc_2 (
    .Select(in_2[1:0]), .Y(l_2_1_demux_2_124803d2_1_l_1_507cfd33), .L_1_bd4f4f3d(L_5_c7845d74),
    .L_2_061b0e56(L_6_a1ac0909), .L_3_85f728ad(L_7_4b7fadd1), .L_0_6365c324(L_4_5ba2c680));
endmodule

module L_8_1_Demux_1_c3500447 (
  input  Y,
  input  [2:0] in_2,
  output L_0_5ac68a80,
  output L_1_ab49ad53,
  output L_2_9682dceb,
  output L_3_c2e8e44e,
  output L_4_5ba2c680,
  output L_5_c7845d74,
  output L_6_a1ac0909,
  output L_7_4b7fadd1
);

  wire l_2_1_demux_1_138d94c5_1_l_0_f163cde3, l_2_1_demux_1_138d94c5_1_l_1_507cfd33;

  L_2_1_Demux_1_138d94c5 l_2_1_demux_1_138d94c5_1 (
    .Select(in_2[2]), .Y(Y), .L_0_f163cde3(l_2_1_demux_1_138d94c5_1_l_0_f163cde3),
    .L_1_507cfd33(l_2_1_demux_1_138d94c5_1_l_1_507cfd33));
  L_4_1_Demux_1_7dcd588f l_4_1_demux_1_7dcd588f_1 (
    .Select(in_2[1:0]), .Y(l_2_1_demux_1_138d94c5_1_l_0_f163cde3), .L_1_bd4f4f3d(L_1_ab49ad53),
    .L_2_061b0e56(L_2_9682dceb), .L_3_85f728ad(L_3_c2e8e44e), .L_0_6365c324(L_0_5ac68a80));
  L_4_1_Demux_1_7dcd588f l_4_1_demux_1_7dcd588f_2 (
    .Select(in_2[1:0]), .Y(l_2_1_demux_1_138d94c5_1_l_1_507cfd33), .L_1_bd4f4f3d(L_5_c7845d74),
    .L_2_061b0e56(L_6_a1ac0909), .L_3_85f728ad(L_7_4b7fadd1), .L_0_6365c324(L_4_5ba2c680));
endmodule
