// Logisim project 1-2 Decoder.circ as structural Verilog: 1 circuit, main circuit L_1_2_Decoder_9aa60696
module L_1_2_Decoder_9aa60696 (
  input  En,
  input  L_0_962f225a,
  output y0,
  output y1
);

  assign y0 = En ? ~L_0_962f225a : 1'bz;  // Controlled_Inverter controlled_inverter_1
  assign y1 = En ? L_0_962f225a : 1'bz;  // Controlled_Buffer controlled_buffer_1

  // Notes on the sheet:
  //   En: pull=down
endmodule
