// Logisim project 2-4 Decoder.circ as structural Verilog: 1 circuit, main circuit 2-4 Decoder
module _2_4_Decoder (
  input  [1:0] Select,
  input  En,
  output y0,
  output y1,
  output y2,
  output y3
);

  wire and_1_out, and_2_out, and_3_out, and_4_out;

  and and_1 (and_1_out, ~Select[1], ~Select[0]);  // AND_Gate
  assign y0 = En ? and_1_out : 1'bz;  // Controlled_Buffer controlled_buffer_1
  and and_2 (and_2_out, ~Select[1], Select[0]);  // AND_Gate
  and and_3 (and_3_out, Select[1], ~Select[0]);  // AND_Gate
  assign y1 = En ? and_2_out : 1'bz;  // Controlled_Buffer controlled_buffer_2
  assign y2 = En ? and_3_out : 1'bz;  // Controlled_Buffer controlled_buffer_3
  and and_4 (and_4_out, Select[1], Select[0]);
  assign y3 = En ? and_4_out : 1'bz;  // Controlled_Buffer controlled_buffer_4

  // Notes on the sheet:
  //   En: pull=down
endmodule
