// Logisim project 3-8 Decoder.circ as structural Verilog: 1 circuit, main circuit L_3_8_Decoder_c117a043
module L_3_8_Decoder_c117a043 (
  input  [2:0] Select,
  input  En,
  output y0,
  output y1,
  output y2,
  output y3,
  output y4,
  output y5,
  output y6,
  output y7
);

  wire and_1_out, and_2_out, and_3_out, and_4_out, and_5_out, and_6_out, and_7_out, and_8_out;

  and and_1 (and_1_out, ~Select[1], ~Select[2], ~Select[0]);  // AND_Gate
  assign y0 = En ? and_1_out : 1'bz;  // Controlled_Buffer controlled_buffer_1
  and and_2 (and_2_out, ~Select[1], ~Select[2], Select[0]);  // AND_Gate
  and and_3 (and_3_out, Select[1], ~Select[2], ~Select[0]);  // AND_Gate
  assign y1 = En ? and_2_out : 1'bz;  // Controlled_Buffer controlled_buffer_2
  assign y2 = En ? and_3_out : 1'bz;  // Controlled_Buffer controlled_buffer_3
  and and_4 (and_4_out, Select[1], ~Select[2], Select[0]);  // AND_Gate
  and and_5 (and_5_out, ~Select[1], Select[2], ~Select[0]);  // AND_Gate
  assign y3 = En ? and_4_out : 1'bz;  // Controlled_Buffer controlled_buffer_4
  assign y4 = En ? and_5_out : 1'bz;  // Controlled_Buffer controlled_buffer_5
  and and_6 (and_6_out, ~Select[1], Select[2], Select[0]);  // AND_Gate
  and and_7 (and_7_out, Select[1], Select[2], ~Select[0]);  // AND_Gate
  assign y5 = En ? and_6_out : 1'bz;  // Controlled_Buffer controlled_buffer_6
  assign y6 = En ? and_7_out : 1'bz;  // Controlled_Buffer controlled_buffer_7
  and and_8 (and_8_out, Select[1], Select[2], Select[0]);
  assign y7 = En ? and_8_out : 1'bz;  // Controlled_Buffer controlled_buffer_8

  // Notes on the sheet:
  //   En: pull=down
endmodule
