// Logisim project 4-16 Decoder.circ as structural Verilog: 1 circuit, main circuit L_4_16_Decoder_e3544e4c
module L_4_16_Decoder_e3544e4c (
  input  [3:0] Select,
  input  En,
  output y0,
  output y1,
  output y2,
  output y3,
  output y4,
  output y5,
  output y6,
  output y7,
  output y8,
  output y9,
  output y10,
  output y11,
  output y12,
  output y13,
  output y14,
  output y15
);

  wire and_1_out, and_2_out, and_3_out, and_4_out, and_5_out, and_6_out, and_7_out, and_8_out, and_9_out,
       and_10_out, and_11_out, and_12_out, and_13_out, and_14_out, and_15_out, and_16_out;

  and and_1 (and_1_out, Select[0], ~Select[1], ~Select[2], ~Select[3]);  // AND_Gate
  and and_2 (and_2_out, ~Select[0], ~Select[1], ~Select[2], ~Select[3]);  // AND_Gate
  assign y1 = En ? and_1_out : 1'bz;  // Controlled_Buffer controlled_buffer_1
  assign y0 = En ? and_2_out : 1'bz;  // Controlled_Buffer controlled_buffer_2
  // NAND_Gate nand_1 is placed but not wired
  and and_3 (and_3_out, ~Select[0], Select[1], ~Select[2], ~Select[3]);  // AND_Gate
  assign y2 = En ? and_3_out : 1'bz;  // Controlled_Buffer controlled_buffer_3
  and and_4 (and_4_out, Select[0], Select[1], ~Select[2], ~Select[3]);  // AND_Gate
  and and_5 (and_5_out, ~Select[0], ~Select[1], Select[2], ~Select[3]);  // AND_Gate
  assign y3 = En ? and_4_out : 1'bz;  // Controlled_Buffer controlled_buffer_4
  assign y4 = En ? and_5_out : 1'bz;  // Controlled_Buffer controlled_buffer_5
  and and_6 (and_6_out, Select[0], ~Select[1], Select[2], ~Select[3]);  // AND_Gate
  and and_7 (and_7_out, ~Select[0], Select[1], Select[2], ~Select[3]);  // AND_Gate
  assign y5 = En ? and_6_out : 1'bz;  // Controlled_Buffer controlled_buffer_6
  assign y6 = En ? and_7_out : 1'bz;  // Controlled_Buffer controlled_buffer_7
  and and_8 (and_8_out, Select[0], Select[1], Select[2], ~Select[3]);  // AND_Gate
  assign y7 = En ? and_8_out : 1'bz;  // Controlled_Buffer controlled_buffer_8
  and and_9 (and_9_out, ~Select[0], ~Select[1], ~Select[2], Select[3]);  // AND_Gate
  and and_10 (and_10_out, Select[0], ~Select[1], ~Select[2], Select[3]);  // AND_Gate
  assign y8 = En ? and_9_out : 1'bz;  // Controlled_Buffer controlled_buffer_9
  assign y9 = En ? and_10_out : 1'bz;  // Controlled_Buffer controlled_buffer_10
  and and_11 (and_11_out, ~Select[0], Select[1], ~Select[2], Select[3]);  // AND_Gate
  assign y10 = En ? and_11_out : 1'bz;  // Controlled_Buffer controlled_buffer_11
  and and_12 (and_12_out, Select[0], Select[1], ~Select[2], Select[3]);  // AND_Gate
  and and_13 (and_13_out, ~Select[0], ~Select[1], Select[2], Select[3]);  // AND_Gate
  assign y11 = En ? and_12_out : 1'bz;  // Controlled_Buffer controlled_buffer_12
  assign y12 = En ? and_13_out : 1'bz;  // Controlled_Buffer controlled_buffer_13
  and and_14 (and_14_out, Select[0], ~Select[1], Select[2], Select[3]);  // AND_Gate
  and and_15 (and_15_out, ~Select[0], Select[1], Select[2], Select[3]);  // AND_Gate
  assign y13 = En ? and_14_out : 1'bz;  // Controlled_Buffer controlled_buffer_14
  assign y14 = En ? and_15_out : 1'bz;  // Controlled_Buffer controlled_buffer_15
  and and_16 (and_16_out, Select[0], Select[1], Select[2], Select[3]);
  assign y15 = En ? and_16_out : 1'bz;  // Controlled_Buffer controlled_buffer_16

  // Notes on the sheet:
  //   En: pull=down
endmodule
