// Logisim project Full Adder.circ as structural Verilog: 5 circuits, main circuit Full_Adder_1_5c6d947c
module Full_Adder_1_5c6d947c (
  input  Cin,
  input  b2,
  input  b1,
  output Sum,
  output Cout
);

  wire and_1_out, and_2_out, xor_1_e881abe8_1_y;

  Xor_1_e881abe8 xor_1_e881abe8_1 (.A(b2), .B(b1), .Y(xor_1_e881abe8_1_y));
  and and_1 (and_1_out, b2, b1);
  Xor_1_e881abe8 xor_1_e881abe8_2 (.A(xor_1_e881abe8_1_y), .B(Cin), .Y(Sum));
  and and_2 (and_2_out, xor_1_e881abe8_1_y, Cin);
  or or_1 (Cout, and_2_out, and_1_out);

  // Notes on the sheet:
  //   Cin: pull=down
endmodule

module Full_Adder_2_7bd0add5 (
  input  Cin,
  input  [1:0] in_2,
  input  [1:0] in_3,
  output [1:0] Sum,
  output Cout
);

  wire full_adder_1_5c6d947c_2_cout;

  Full_Adder_1_5c6d947c full_adder_1_5c6d947c_1 (
    .Cin(full_adder_1_5c6d947c_2_cout), .b1(in_2[1]), .b2(in_3[1]), .Sum(Sum[1]), .Cout(Cout));
  Full_Adder_1_5c6d947c full_adder_1_5c6d947c_2 (
    .Cin(Cin), .b1(in_2[0]), .b2(in_3[0]), .Sum(Sum[0]), .Cout(full_adder_1_5c6d947c_2_cout));

  // Notes on the sheet:
  //   Cin: pull=down
endmodule

module Full_Adder_4_e2d4d40b (
  input  Cin,
  input  [3:0] in_2,
  input  [3:0] in_3,
  output [3:0] Sum,
  output Cout
);

  wire full_adder_1_5c6d947c_2_cout, full_adder_1_5c6d947c_3_cout, full_adder_1_5c6d947c_4_cout;

  Full_Adder_1_5c6d947c full_adder_1_5c6d947c_1 (
    .Cin(full_adder_1_5c6d947c_2_cout), .b1(in_2[3]), .b2(in_3[3]), .Sum(Sum[3]), .Cout(Cout));
  Full_Adder_1_5c6d947c full_adder_1_5c6d947c_2 (
    .Cin(full_adder_1_5c6d947c_3_cout), .b1(in_2[2]), .b2(in_3[2]), .Sum(Sum[2]),
    .Cout(full_adder_1_5c6d947c_2_cout));
  Full_Adder_1_5c6d947c full_adder_1_5c6d947c_3 (
    .Cin(full_adder_1_5c6d947c_4_cout), .b1(in_2[1]), .b2(in_3[1]), .Sum(Sum[1]),
    .Cout(full_adder_1_5c6d947c_3_cout));
  Full_Adder_1_5c6d947c full_adder_1_5c6d947c_4 (
    .Cin(Cin), .b1(in_2[0]), .b2(in_3[0]), .Sum(Sum[0]), .Cout(full_adder_1_5c6d947c_4_cout));

  // Notes on the sheet:
  //   Cin: pull=down
endmodule

module Full_Adder_8_b59b4ad2 (
  input  Cin,
  input  [7:0] in_2,
  input  [7:0] in_3,
  output [7:0] Sum,
  output Cout
);

  wire full_adder_1_5c6d947c_2_cout, full_adder_1_5c6d947c_3_cout, full_adder_1_5c6d947c_4_cout,
       full_adder_1_5c6d947c_5_cout, full_adder_1_5c6d947c_6_cout, full_adder_1_5c6d947c_7_cout,
       full_adder_1_5c6d947c_8_cout;

  Full_Adder_1_5c6d947c full_adder_1_5c6d947c_1 (
    .Cin(full_adder_1_5c6d947c_2_cout), .b1(in_2[7]), .b2(in_3[7]), .Sum(Sum[7]), .Cout(Cout));
  Full_Adder_1_5c6d947c full_adder_1_5c6d947c_2 (
    .Cin(full_adder_1_5c6d947c_3_cout), .b1(in_2[6]), .b2(in_3[6]), .Sum(Sum[6]),
    .Cout(full_adder_1_5c6d947c_2_cout));
  Full_Adder_1_5c6d947c full_adder_1_5c6d947c_3 (
    .Cin(full_adder_1_5c6d947c_4_cout), .b1(in_2[5]), .b2(in_3[5]), .Sum(Sum[5]),
    .Cout(full_adder_1_5c6d947c_3_cout));
  Full_Adder_1_5c6d947c full_adder_1_5c6d947c_4 (
    .Cin(full_adder_1_5c6d947c_5_cout), .b1(in_2[4]), .b2(in_3[4]), .Sum(Sum[4]),
    .Cout(full_adder_1_5c6d947c_4_cout));
  Full_Adder_1_5c6d947c full_adder_1_5c6d947c_5 (
    .Cin(full_adder_1_5c6d947c_6_cout), .b1(in_2[3]), .b2(in_3[3]), .Sum(Sum[3]),
    .Cout(full_adder_1_5c6d947c_5_cout));
  Full_Adder_1_5c6d947c full_adder_1_5c6d947c_6 (
    .Cin(full_adder_1_5c6d947c_7_cout), .b1(in_2[2]), .b2(in_3[2]), .Sum(Sum[2]),
    .Cout(full_adder_1_5c6d947c_6_cout));
  Full_Adder_1_5c6d947c full_adder_1_5c6d947c_7 (
    .Cin(full_adder_1_5c6d947c_8_cout), .b1(in_2[1]), .b2(in_3[1]), .Sum(Sum[1]),
    .Cout(full_adder_1_5c6d947c_7_cout));
  Full_Adder_1_5c6d947c full_adder_1_5c6d947c_8 (
    .Cin(Cin), .b1(in_2[0]), .b2(in_3[0]), .Sum(Sum[0]), .Cout(full_adder_1_5c6d947c_8_cout));

  // Notes on the sheet:
  //   Cin: pull=down
endmodule

module Full_Adder_16_8a49bf5a (
  input  Cin,
  input  [15:0] A,
  input  [15:0] B,
  output [15:0] Sum,
  output Cout
);

  wire full_adder_8_b59b4ad2_2_cout;

  Full_Adder_8_b59b4ad2 full_adder_8_b59b4ad2_1 (
    .in_2(A[15:8]), .in_3(B[15:8]), .Cin(full_adder_8_b59b4ad2_2_cout), .Sum(Sum[15:8]), .Cout(Cout));
  Full_Adder_8_b59b4ad2 full_adder_8_b59b4ad2_2 (
    .in_2(A[7:0]), .in_3(B[7:0]), .Cin(Cin), .Sum(Sum[7:0]), .Cout(full_adder_8_b59b4ad2_2_cout));

  // Notes on the sheet:
  //   Cin: pull=down
endmodule
