// Logisim project Error Detect.circ as structural Verilog: 5 circuits, main circuit Error_Detector_16_c93c636a
module Error_Detector_16_c93c636a (
  input  [15:0] In,
  output [15:0] Out
);

  wire [15:0] and_1_out, and_2_out, error_to_high_16_aba480bc_1_out, error_to_low_16_a6e62caa_1_out;

  Pull_Resistor pull_resistor_1 (.node(In));
  Error_to_high_16_aba480bc error_to_high_16_aba480bc_1 (.In(In), .Out(error_to_high_16_aba480bc_1_out));
  Error_to_low_16_a6e62caa error_to_low_16_a6e62caa_1 (.In(In), .Out(error_to_low_16_a6e62caa_1_out));
  assign and_1_out = ~error_to_low_16_a6e62caa_1_out & ~error_to_high_16_aba480bc_1_out;  // AND_Gate and_1, 16 bits wide
  assign and_2_out = error_to_low_16_a6e62caa_1_out & error_to_high_16_aba480bc_1_out;  // AND_Gate and_2, 16 bits wide
  assign Out = ~(and_1_out | and_2_out);  // NOR_Gate nor_1, 16 bits wide

  // Notes on the sheet:
  //   Works by using pull behavior to set logic
  //   Only outputs 1 on Error input
endmodule

module Error_Detector_8_b862b878 (
  input  [7:0] In,
  output [7:0] Out
);

  wire [7:0] and_1_out, and_2_out, error_to_high_8_255a56c3_1_out, error_to_low_8_10258360_1_out;

  Pull_Resistor pull_resistor_1 (.node(In));
  Error_to_high_8_255a56c3 error_to_high_8_255a56c3_1 (.In(In), .Out(error_to_high_8_255a56c3_1_out));
  Error_to_low_8_10258360 error_to_low_8_10258360_1 (.In(In), .Out(error_to_low_8_10258360_1_out));
  assign and_1_out = ~error_to_low_8_10258360_1_out & ~error_to_high_8_255a56c3_1_out;  // AND_Gate and_1, 8 bits wide
  assign and_2_out = error_to_low_8_10258360_1_out & error_to_high_8_255a56c3_1_out;  // AND_Gate and_2, 8 bits wide
  assign Out = ~(and_1_out | and_2_out);  // NOR_Gate nor_1, 8 bits wide

  // Notes on the sheet:
  //   Works by using pull behavior to set logic
  //   Only outputs 1 on Error input
endmodule

module Error_Detector_4_19cb23b6 (
  input  [3:0] In,
  output [3:0] Out
);

  wire [3:0] and_1_out, and_2_out, error_to_high_4_049c0a9e_1_out, error_to_low_4_56fc822c_1_out;

  Pull_Resistor pull_resistor_1 (.node(In));
  Error_to_high_4_049c0a9e error_to_high_4_049c0a9e_1 (.In(In), .Out(error_to_high_4_049c0a9e_1_out));
  Error_to_low_4_56fc822c error_to_low_4_56fc822c_1 (.In(In), .Out(error_to_low_4_56fc822c_1_out));
  assign and_1_out = ~error_to_low_4_56fc822c_1_out & ~error_to_high_4_049c0a9e_1_out;  // AND_Gate and_1, 4 bits wide
  assign and_2_out = error_to_low_4_56fc822c_1_out & error_to_high_4_049c0a9e_1_out;  // AND_Gate and_2, 4 bits wide
  assign Out = ~(and_1_out | and_2_out);  // NOR_Gate nor_1, 4 bits wide

  // Notes on the sheet:
  //   Works by using pull behavior to set logic
  //   Only outputs 1 on Error input
endmodule

module Error_Detector_2_075d48e1 (
  input  [1:0] In,
  output [1:0] Out
);

  wire [1:0] and_1_out, and_2_out, error_to_high_2_3705d205_1_out, error_to_low_2_4d295280_1_out;

  Pull_Resistor pull_resistor_1 (.node(In));
  Error_to_high_2_3705d205 error_to_high_2_3705d205_1 (.In(In), .Out(error_to_high_2_3705d205_1_out));
  Error_to_low_2_4d295280 error_to_low_2_4d295280_1 (.In(In), .Out(error_to_low_2_4d295280_1_out));
  assign and_1_out = ~error_to_low_2_4d295280_1_out & ~error_to_high_2_3705d205_1_out;  // AND_Gate and_1, 2 bits wide
  assign and_2_out = error_to_low_2_4d295280_1_out & error_to_high_2_3705d205_1_out;  // AND_Gate and_2, 2 bits wide
  assign Out = ~(and_1_out | and_2_out);  // NOR_Gate nor_1, 2 bits wide

  // Notes on the sheet:
  //   Works by using pull behavior to set logic
  //   Only outputs 1 on Error input
endmodule

module Error_Detector_1_dbfb092c (
  input  In,
  output Out
);

  wire and_1_out, and_2_out, error_to_high_1_d72b71e8_1_out, error_to_low_1_b2f6d6ef_1_out;

  Pull_Resistor pull_resistor_1 (.node(In));
  Error_to_high_1_d72b71e8 error_to_high_1_d72b71e8_1 (.In(In), .Out(error_to_high_1_d72b71e8_1_out));
  Error_to_low_1_b2f6d6ef error_to_low_1_b2f6d6ef_1 (.In(In), .Out(error_to_low_1_b2f6d6ef_1_out));
  and and_1 (and_1_out, ~error_to_low_1_b2f6d6ef_1_out, ~error_to_high_1_d72b71e8_1_out);  // AND_Gate
  and and_2 (and_2_out, error_to_low_1_b2f6d6ef_1_out, error_to_high_1_d72b71e8_1_out);
  nor nor_1 (Out, and_1_out, and_2_out);

  // Notes on the sheet:
  //   Works by using pull behavior to set logic
  //   Only outputs 1 on Error input
endmodule
