// Logisim project Error to High.circ as structural Verilog: 5 circuits, main circuit Error_to_high_16_aba480bc
module Error_to_high_16_aba480bc (
  input  [15:0] In,
  output [15:0] Out
);


  assign Out = In;

  // Notes on the sheet:
  //   In: pull=up
  //   Only overrides Error input
  //   Works by using pull behavior to set logic
  //   Since input is tristate, it accepts tristate input as well.
endmodule

module Error_to_high_8_255a56c3 (
  input  [7:0] In,
  output [7:0] Out
);


  assign Out = In;

  // Notes on the sheet:
  //   In: pull=up
  //   Only overrides Error input
  //   Works by using pull behavior to set logic
  //   Since input is tristate, it accepts tristate input as well.
endmodule

module Error_to_high_4_049c0a9e (
  input  [3:0] In,
  output [3:0] Out
);


  assign Out = In;

  // Notes on the sheet:
  //   In: pull=up
  //   Only overrides Error input
  //   Works by using pull behavior to set logic
  //   Since input is tristate, it accepts tristate input as well.
endmodule

module Error_to_high_2_3705d205 (
  input  [1:0] In,
  output [1:0] Out
);


  assign Out = In;

  // Notes on the sheet:
  //   In: pull=up
  //   Only overrides Error input
  //   Works by using pull behavior to set logic
  //   Since input is tristate, it accepts tristate input as well.
endmodule

module Error_to_high_1_d72b71e8 (
  input  In,
  output Out
);


  assign Out = In;

  // Notes on the sheet:
  //   In: pull=up
  //   Only overrides Error input
  //   Works by using pull behavior to set logic
  //   Since input is tristate, it accepts tristate input as well.
endmodule
