// Logisim project Error to Low.circ as structural Verilog: 5 circuits, main circuit Error_to_low_16_a6e62caa
module Error_to_low_16_a6e62caa (
  input  [15:0] In,
  output [15:0] Out
);


  assign Out = In;

  // Notes on the sheet:
  //   In: pull=down
  //   Only overrides Error input
  //   Works by using pull behavior to set logic
  //   Since input is tristate, it accepts tristate input as well.
endmodule

module Error_to_low_8_10258360 (
  input  [7:0] In,
  output [7:0] Out
);


  assign Out = In;

  // Notes on the sheet:
  //   In: pull=down
  //   Only overrides Error input
  //   Works by using pull behavior to set logic
  //   Since input is tristate, it accepts tristate input as well.
endmodule

module Error_to_low_4_56fc822c (
  input  [3:0] In,
  output [3:0] Out
);


  assign Out = In;

  // Notes on the sheet:
  //   In: pull=down
  //   Only overrides Error input
  //   Works by using pull behavior to set logic
  //   Since input is tristate, it accepts tristate input as well.
endmodule

module Error_to_low_2_4d295280 (
  input  [1:0] In,
  output [1:0] Out
);


  assign Out = In;

  // Notes on the sheet:
  //   In: pull=down
  //   Only overrides Error input
  //   Works by using pull behavior to set logic
  //   Since input is tristate, it accepts tristate input as well.
endmodule

module Error_to_low_1_b2f6d6ef (
  input  In,
  output Out
);


  assign Out = In;

  // Notes on the sheet:
  //   In: pull=down
  //   Only overrides Error input
  //   Works by using pull behavior to set logic
  //   Since input is tristate, it accepts tristate input as well.
endmodule
