// Logisim project Error to Z.circ as structural Verilog: 5 circuits, main circuit Error_to_Z_16_880f2035
module Error_to_Z_16_880f2035 (
  input  [15:0] In,
  output [15:0] Out
);

  wire error_detector_1_dbfb092c_1_out, not_1_out;

  not not_1 (not_1_out, error_detector_1_dbfb092c_1_out);
  Error_Detector_1_dbfb092c error_detector_1_dbfb092c_1 (.In(In[0]), .Out(error_detector_1_dbfb092c_1_out));
  assign Out = not_1_out ? In : 16'bz;  // Controlled_Buffer controlled_buffer_1

  // Notes on the sheet:
  //   Only overrides Error input
  //   Since input is tristate, it accepts tristate input as well.
endmodule

module Error_to_Z_8_79ae8b3f (
  input  [7:0] In,
  output [7:0] Out
);

  wire error_detector_1_dbfb092c_1_out, not_1_out;

  not not_1 (not_1_out, error_detector_1_dbfb092c_1_out);
  Error_Detector_1_dbfb092c error_detector_1_dbfb092c_1 (.In(In[0]), .Out(error_detector_1_dbfb092c_1_out));
  assign Out = not_1_out ? In : 8'bz;  // Controlled_Buffer controlled_buffer_1

  // Notes on the sheet:
  //   Only overrides Error input
  //   Since input is tristate, it accepts tristate input as well.
endmodule

module Error_to_Z_4_c94d2830 (
  input  [3:0] In,
  output [3:0] Out
);

  wire error_detector_1_dbfb092c_1_out, not_1_out;

  Error_Detector_1_dbfb092c error_detector_1_dbfb092c_1 (.In(In[0]), .Out(error_detector_1_dbfb092c_1_out));
  not not_1 (not_1_out, error_detector_1_dbfb092c_1_out);
  assign Out = not_1_out ? In : 4'bz;  // Controlled_Buffer controlled_buffer_1

  // Notes on the sheet:
  //   Only overrides Error input
  //   Since input is tristate, it accepts tristate input as well.
endmodule

module Error_to_Z_2_333e3e04 (
  input  [1:0] In,
  output [1:0] Out
);

  wire error_detector_1_dbfb092c_1_out, not_1_out;

  Error_Detector_1_dbfb092c error_detector_1_dbfb092c_1 (.In(In[0]), .Out(error_detector_1_dbfb092c_1_out));
  not not_1 (not_1_out, error_detector_1_dbfb092c_1_out);
  assign Out = not_1_out ? In : 2'bz;  // Controlled_Buffer controlled_buffer_1

  // Notes on the sheet:
  //   Only overrides Error input
  //   Since input is tristate, it accepts tristate input as well.
endmodule

module Error_to_Z_1_d19dd860 (
  input  In,
  output Out
);

  wire error_detector_1_dbfb092c_1_out, not_1_out;

  Error_Detector_1_dbfb092c error_detector_1_dbfb092c_1 (.In(In), .Out(error_detector_1_dbfb092c_1_out));
  not not_1 (not_1_out, error_detector_1_dbfb092c_1_out);
  assign Out = not_1_out ? In : 1'bz;  // Controlled_Buffer controlled_buffer_1

  // Notes on the sheet:
  //   Only overrides Error input
  //   Since input is tristate, it accepts tristate input as well.
endmodule
