// Logisim project 16-1 Mux.circ as structural Verilog: 5 circuits, main circuit 16-1 Mux (8)
module _16_1_Mux__16 (
  input  [15:0] _0,
  input  [15:0] _15,
  input  [15:0] _1,
  input  [15:0] _14,
  input  [15:0] _2,
  input  [15:0] _13,
  input  [15:0] _3,
  input  [15:0] _12,
  input  [15:0] _4,
  input  [15:0] _11,
  input  [15:0] _5,
  input  [15:0] _10,
  input  [15:0] _6,
  input  [15:0] _9,
  input  [15:0] _7,
  input  [15:0] _8,
  input  [3:0] in_17,
  output [15:0] out_18
);

  wire [15:0] n8_1_mux_16_1_out_10, n8_1_mux_16_2_out_10;

  _8_1_Mux__16 u_8_1_mux_16_1 (
    ._0(_0), ._1(_1), ._2(_2), ._3(_3), ._4(_4), ._5(_5), ._6(_6), ._7(_7), .in_9(in_17[2:0]),
    .out_10(n8_1_mux_16_1_out_10));
  _2_1_Mux__16 u_2_1_mux_16_1 (._0(n8_1_mux_16_1_out_10), ._1(n8_1_mux_16_2_out_10), .Select(in_17[3]), .Y(out_18));
  _8_1_Mux__16 u_8_1_mux_16_2 (
    ._0(_8), ._1(_9), ._2(_10), ._3(_11), ._4(_12), ._5(_13), ._6(_14), ._7(_15), .in_9(in_17[2:0]),
    .out_10(n8_1_mux_16_2_out_10));
endmodule

module _16_1_Mux__8 (
  input  [7:0] _0,
  input  [7:0] _1,
  input  [7:0] _2,
  input  [7:0] _3,
  input  [7:0] _4,
  input  [7:0] _5,
  input  [7:0] _6,
  input  [7:0] _7,
  input  [7:0] _8,
  input  [7:0] _9,
  input  [7:0] _10,
  input  [7:0] _11,
  input  [7:0] _12,
  input  [7:0] _13,
  input  [7:0] _14,
  input  [3:0] in_16,
  input  [7:0] _15,
  output [7:0] out_18
);

  wire [7:0] n8_1_mux_8_1_out_10, n8_1_mux_8_2_out_10;

  _8_1_Mux__8 u_8_1_mux_8_1 (
    ._0(_0), ._1(_1), ._2(_2), ._3(_3), ._4(_4), ._5(_5), ._6(_6), ._7(_7), .in_9(in_16[2:0]),
    .out_10(n8_1_mux_8_1_out_10));
  _8_1_Mux__8 u_8_1_mux_8_2 (
    ._0(_8), ._1(_9), ._2(_10), ._3(_11), ._4(_12), ._5(_13), ._6(_14), ._7(_15), .in_9(in_16[2:0]),
    .out_10(n8_1_mux_8_2_out_10));
  _2_1_Mux__8 u_2_1_mux_8_1 (._1(n8_1_mux_8_2_out_10), ._0(n8_1_mux_8_1_out_10), .Select(in_16[3]), .Y(out_18));
endmodule

module _16_1_Mux__4 (
  input  [3:0] _0,
  input  [3:0] _1,
  input  [3:0] _2,
  input  [3:0] _3,
  input  [3:0] _4,
  input  [3:0] _5,
  input  [3:0] _6,
  input  [3:0] _7,
  input  [3:0] _8,
  input  [3:0] _9,
  input  [3:0] _10,
  input  [3:0] _11,
  input  [3:0] _12,
  input  [3:0] _13,
  input  [3:0] _14,
  input  [3:0] in_16,
  input  [3:0] _15,
  output [3:0] out_18
);

  wire [3:0] n8_1_mux_4_1_out_10, n8_1_mux_4_2_out_10;

  _8_1_Mux__4 u_8_1_mux_4_1 (
    ._0(_0), ._1(_1), ._2(_2), ._3(_3), ._4(_4), ._5(_5), ._6(_6), ._7(_7), .in_9(in_16[2:0]),
    .out_10(n8_1_mux_4_1_out_10));
  _8_1_Mux__4 u_8_1_mux_4_2 (
    ._0(_8), ._1(_9), ._2(_10), ._3(_11), ._4(_12), ._5(_13), ._6(_14), ._7(_15), .in_9(in_16[2:0]),
    .out_10(n8_1_mux_4_2_out_10));
  _2_1_Mux__4 u_2_1_mux_4_1 (._0(n8_1_mux_4_1_out_10), ._1(n8_1_mux_4_2_out_10), .Select(in_16[3]), .Y(out_18));
endmodule

module _16_1_Mux__2 (
  input  [1:0] _0,
  input  [1:0] _1,
  input  [1:0] _2,
  input  [1:0] _3,
  input  [1:0] _4,
  input  [1:0] _5,
  input  [1:0] _6,
  input  [1:0] _7,
  input  [1:0] _8,
  input  [1:0] _9,
  input  [1:0] _10,
  input  [1:0] _11,
  input  [1:0] _12,
  input  [1:0] _13,
  input  [1:0] _14,
  input  [3:0] in_16,
  input  [1:0] _15,
  output [1:0] out_18
);

  wire [1:0] n8_1_mux_2_1_out_10, n8_1_mux_2_2_out_10;

  _8_1_Mux__2 u_8_1_mux_2_1 (
    ._0(_0), ._1(_1), ._2(_2), ._3(_3), ._4(_4), ._5(_5), ._6(_6), ._7(_7), .in_9(in_16[2:0]),
    .out_10(n8_1_mux_2_1_out_10));
  _8_1_Mux__2 u_8_1_mux_2_2 (
    ._0(_8), ._1(_9), ._2(_10), ._3(_11), ._4(_12), ._5(_13), ._6(_14), ._7(_15), .in_9(in_16[2:0]),
    .out_10(n8_1_mux_2_2_out_10));
  _2_1_Mux__2 u_2_1_mux_2_1 (._0(n8_1_mux_2_1_out_10), ._1(n8_1_mux_2_2_out_10), .Select(in_16[3]), .Y(out_18));
endmodule

module _16_1_Mux__1 (
  input  _0,
  input  _1,
  input  _2,
  input  _3,
  input  _4,
  input  _5,
  input  _6,
  input  _7,
  input  _8,
  input  _9,
  input  _10,
  input  _11,
  input  _12,
  input  _13,
  input  _14,
  input  [3:0] in_16,
  input  _15,
  output out_18
);

  wire n8_1_mux_1_1_out_10, n8_1_mux_1_2_out_10;

  _8_1_Mux__1 u_8_1_mux_1_1 (
    ._0(_0), ._1(_1), ._2(_2), ._3(_3), ._4(_4), ._5(_5), ._6(_6), ._7(_7), .in_9(in_16[2:0]),
    .out_10(n8_1_mux_1_1_out_10));
  _8_1_Mux__1 u_8_1_mux_1_2 (
    ._0(_8), ._1(_9), ._2(_10), ._3(_11), ._4(_12), ._5(_13), ._6(_14), ._7(_15), .in_9(in_16[2:0]),
    .out_10(n8_1_mux_1_2_out_10));
  _2_1_Mux__1 u_2_1_mux_1_1 (._0(n8_1_mux_1_1_out_10), ._1(n8_1_mux_1_2_out_10), .Select(in_16[3]), .Y(out_18));
endmodule
