// Logisim project 2-1 Demux.circ as structural Verilog: 5 circuits, main circuit Demux_16
module Demux_16 (
  input  [15:0] Y,
  input  Select,
  output [15:0] p0,
  output [15:0] p1
);

  wire not_1_out;

  assign p0 = not_1_out ? Y : 16'bz;  // Controlled_Buffer controlled_buffer_1
  not not_1 (not_1_out, Select);
  assign p1 = Select ? Y : 16'bz;  // Controlled_Buffer controlled_buffer_2
endmodule

module Demux_8 (
  input  [7:0] Y,
  input  Select,
  output [7:0] p0,
  output [7:0] p1
);

  wire not_1_out;

  assign p0 = not_1_out ? Y : 8'bz;  // Controlled_Buffer controlled_buffer_1
  not not_1 (not_1_out, Select);
  assign p1 = Select ? Y : 8'bz;  // Controlled_Buffer controlled_buffer_2
endmodule

module Demux_4 (
  input  [3:0] Y,
  input  Select,
  output [3:0] p0,
  output [3:0] p1
);

  wire not_1_out;

  assign p0 = not_1_out ? Y : 4'bz;  // Controlled_Buffer controlled_buffer_1
  not not_1 (not_1_out, Select);
  assign p1 = Select ? Y : 4'bz;  // Controlled_Buffer controlled_buffer_2
endmodule

module Demux_2 (
  input  [1:0] Y,
  input  Select,
  output [1:0] p0,
  output [1:0] p1
);

  wire not_1_out;

  assign p0 = not_1_out ? Y : 2'bz;  // Controlled_Buffer controlled_buffer_1
  not not_1 (not_1_out, Select);
  assign p1 = Select ? Y : 2'bz;  // Controlled_Buffer controlled_buffer_2
endmodule

module Demux_1 (
  input  Y,
  input  Select,
  output p0,
  output p1
);

  wire not_1_out;

  assign p0 = not_1_out ? Y : 1'bz;  // Controlled_Buffer controlled_buffer_1
  not not_1 (not_1_out, Select);
  assign p1 = Select ? Y : 1'bz;  // Controlled_Buffer controlled_buffer_2
endmodule
