// Logisim project 2-1 Mux.circ as structural Verilog: 5 circuits, main circuit 2-1 Mux (8)
module _2_1_Mux__16 (
  input  [15:0] _0,
  input  [15:0] _1,
  input  Select,
  output [15:0] Y
);

  wire [15:0] and_1_out, and_2_out, not_1_out, or_1_out;

  assign not_1_out = ~{16{Select}};  // NOT_Gate not_1, 16 bits wide
  assign and_1_out = _0 & not_1_out;  // AND_Gate and_1, 16 bits wide
  assign and_2_out = _1 & {16{Select}};  // AND_Gate and_2, 16 bits wide
  Error_to_Z__16 error_to_z_16_1 (.In(or_1_out), .Out(Y));
  assign or_1_out = and_1_out | and_2_out;  // OR_Gate or_1, 16 bits wide
endmodule

module _2_1_Mux__8 (
  input  [7:0] _0,
  input  [7:0] _1,
  input  Select,
  output [7:0] Y
);

  wire [7:0] and_1_out, and_2_out, not_1_out, or_1_out;

  assign not_1_out = ~{8{Select}};  // NOT_Gate not_1, 8 bits wide
  assign and_1_out = _0 & not_1_out;  // AND_Gate and_1, 8 bits wide
  assign and_2_out = _1 & {8{Select}};  // AND_Gate and_2, 8 bits wide
  assign or_1_out = and_1_out | and_2_out;  // OR_Gate or_1, 8 bits wide
  Error_to_Z__8 error_to_z_8_1 (.In(or_1_out), .Out(Y));
endmodule

module _2_1_Mux__4 (
  input  [3:0] _0,
  input  [3:0] _1,
  input  Select,
  output [3:0] Y
);

  wire [3:0] and_1_out, and_2_out, not_1_out, or_1_out;

  assign not_1_out = ~{4{Select}};  // NOT_Gate not_1, 4 bits wide
  assign and_1_out = _0 & not_1_out;  // AND_Gate and_1, 4 bits wide
  assign and_2_out = _1 & {4{Select}};  // AND_Gate and_2, 4 bits wide
  Error_to_Z__4 error_to_z_4_1 (.In(or_1_out), .Out(Y));
  assign or_1_out = and_1_out | and_2_out;  // OR_Gate or_1, 4 bits wide
endmodule

module _2_1_Mux__2 (
  input  [1:0] _0,
  input  [1:0] _1,
  input  Select,
  output [1:0] Y
);

  wire [1:0] and_1_out, and_2_out, not_1_out, or_1_out;

  assign not_1_out = ~{2{Select}};  // NOT_Gate not_1, 2 bits wide
  assign and_1_out = _0 & not_1_out;  // AND_Gate and_1, 2 bits wide
  assign and_2_out = _1 & {2{Select}};  // AND_Gate and_2, 2 bits wide
  Error_to_Z__2 error_to_z_2_1 (.In(or_1_out), .Out(Y));
  assign or_1_out = and_1_out | and_2_out;  // OR_Gate or_1, 2 bits wide
endmodule

module _2_1_Mux__1 (
  input  _0,
  input  _1,
  input  Select,
  output Y
);

  wire and_1_out, and_2_out, not_1_out, or_1_out;

  not not_1 (not_1_out, Select);
  and and_1 (and_1_out, _0, not_1_out);
  and and_2 (and_2_out, _1, Select);
  Error_to_Z__1 error_to_z_1_1 (.In(or_1_out), .Out(Y));
  or or_1 (or_1_out, and_1_out, and_2_out);
endmodule
