// Logisim project 4-1 Mux.circ as structural Verilog: 5 circuits, main circuit 4-1 Mux (8)
module _4_1_Mux__16 (
  input  [15:0] _0,
  input  [15:0] _1,
  input  [15:0] _2,
  input  [15:0] _3,
  input  [1:0] Select,
  output [15:0] Y
);

  wire [15:0] and_1_out, and_2_out, and_3_out, and_4_out, not_1_out, not_2_out, not_3_out, not_4_out,
       or_1_out;

  assign not_1_out = ~{16{Select[0]}};  // NOT_Gate not_1, 16 bits wide
  assign not_2_out = ~{16{Select[1]}};  // NOT_Gate not_2, 16 bits wide
  assign not_3_out = ~{16{Select[0]}};  // NOT_Gate not_3, 16 bits wide
  assign not_4_out = ~{16{Select[1]}};  // NOT_Gate not_4, 16 bits wide
  assign and_1_out = _0 & not_1_out & not_2_out;  // AND_Gate and_1, 16 bits wide
  assign and_2_out = _2 & not_3_out & {16{Select[1]}};  // AND_Gate and_2, 16 bits wide
  assign and_3_out = _1 & {16{Select[0]}} & not_4_out;  // AND_Gate and_3, 16 bits wide
  assign and_4_out = _3 & {16{Select[0]}} & {16{Select[1]}};  // AND_Gate and_4, 16 bits wide
  assign or_1_out = and_1_out | and_2_out | and_3_out | and_4_out;  // OR_Gate or_1, 16 bits wide
  Error_to_Z__16 error_to_z_16_1 (.In(or_1_out), .Out(Y));
endmodule

module _4_1_Mux__8 (
  input  [7:0] _0,
  input  [7:0] _1,
  input  [7:0] _2,
  input  [7:0] _3,
  input  [1:0] Select,
  output [7:0] Y
);

  wire [7:0] and_1_out, and_2_out, and_3_out, and_4_out, not_1_out, not_2_out, not_3_out, not_4_out, or_1_out;

  assign not_1_out = ~{8{Select[0]}};  // NOT_Gate not_1, 8 bits wide
  assign not_2_out = ~{8{Select[1]}};  // NOT_Gate not_2, 8 bits wide
  assign not_3_out = ~{8{Select[0]}};  // NOT_Gate not_3, 8 bits wide
  assign not_4_out = ~{8{Select[1]}};  // NOT_Gate not_4, 8 bits wide
  assign and_1_out = _0 & not_1_out & not_2_out;  // AND_Gate and_1, 8 bits wide
  assign and_2_out = _2 & not_3_out & {8{Select[1]}};  // AND_Gate and_2, 8 bits wide
  assign and_3_out = _1 & {8{Select[0]}} & not_4_out;  // AND_Gate and_3, 8 bits wide
  assign and_4_out = _3 & {8{Select[0]}} & {8{Select[1]}};  // AND_Gate and_4, 8 bits wide
  Error_to_Z__8 error_to_z_8_1 (.In(or_1_out), .Out(Y));
  assign or_1_out = and_1_out | and_2_out | and_3_out | and_4_out;  // OR_Gate or_1, 8 bits wide
endmodule

module _4_1_Mux__4 (
  input  [3:0] _0,
  input  [3:0] _1,
  input  [3:0] _2,
  input  [3:0] _3,
  input  [1:0] Select,
  output [3:0] Y
);

  wire [3:0] and_1_out, and_2_out, and_3_out, and_4_out, not_1_out, not_2_out, not_3_out, not_4_out, or_1_out;

  assign not_1_out = ~{4{Select[0]}};  // NOT_Gate not_1, 4 bits wide
  assign not_2_out = ~{4{Select[1]}};  // NOT_Gate not_2, 4 bits wide
  assign not_3_out = ~{4{Select[0]}};  // NOT_Gate not_3, 4 bits wide
  assign not_4_out = ~{4{Select[1]}};  // NOT_Gate not_4, 4 bits wide
  assign and_1_out = _0 & not_1_out & not_2_out;  // AND_Gate and_1, 4 bits wide
  assign and_2_out = _2 & not_3_out & {4{Select[1]}};  // AND_Gate and_2, 4 bits wide
  assign and_3_out = _1 & {4{Select[0]}} & not_4_out;  // AND_Gate and_3, 4 bits wide
  assign and_4_out = _3 & {4{Select[0]}} & {4{Select[1]}};  // AND_Gate and_4, 4 bits wide
  assign or_1_out = and_1_out | and_2_out | and_3_out | and_4_out;  // OR_Gate or_1, 4 bits wide
  Error_to_Z__4 error_to_z_4_1 (.In(or_1_out), .Out(Y));
endmodule

module _4_1_Mux__2 (
  input  [1:0] _0,
  input  [1:0] _1,
  input  [1:0] _2,
  input  [1:0] _3,
  input  [1:0] Select,
  output [1:0] Y
);

  wire [1:0] and_1_out, and_2_out, and_3_out, and_4_out, not_1_out, not_2_out, not_3_out, not_4_out, or_1_out;

  assign not_1_out = ~{2{Select[0]}};  // NOT_Gate not_1, 2 bits wide
  assign not_2_out = ~{2{Select[1]}};  // NOT_Gate not_2, 2 bits wide
  assign not_3_out = ~{2{Select[0]}};  // NOT_Gate not_3, 2 bits wide
  assign not_4_out = ~{2{Select[1]}};  // NOT_Gate not_4, 2 bits wide
  assign and_1_out = _0 & not_1_out & not_2_out;  // AND_Gate and_1, 2 bits wide
  assign and_2_out = _2 & not_3_out & {2{Select[1]}};  // AND_Gate and_2, 2 bits wide
  assign and_3_out = _1 & {2{Select[0]}} & not_4_out;  // AND_Gate and_3, 2 bits wide
  assign and_4_out = _3 & {2{Select[0]}} & {2{Select[1]}};  // AND_Gate and_4, 2 bits wide
  assign or_1_out = and_1_out | and_2_out | and_3_out | and_4_out;  // OR_Gate or_1, 2 bits wide
  Error_to_Z__2 error_to_z_2_1 (.In(or_1_out), .Out(Y));
endmodule

module _4_1_Mux__1 (
  input  _0,
  input  _1,
  input  _2,
  input  _3,
  input  [1:0] Select,
  output Y
);

  wire and_1_out, and_2_out, and_3_out, and_4_out, not_1_out, not_2_out, not_3_out, not_4_out, or_1_out,
       undriven;

  not not_1 (not_1_out, Select[0]);
  not not_2 (not_2_out, Select[1]);
  not not_3 (not_3_out, Select[0]);
  not not_4 (not_4_out, Select[1]);
  and and_1 (and_1_out, _0, not_1_out, not_2_out);
  and and_2 (and_2_out, undriven, not_3_out, Select[1]);
  and and_3 (and_3_out, _1, Select[0], not_4_out);
  and and_4 (and_4_out, _3, Select[0], Select[1]);
  or or_1 (or_1_out, and_1_out, and_2_out, and_3_out, and_4_out);
  Error_to_Z__1 error_to_z_1_1 (.In(or_1_out), .Out(Y));
endmodule
