// Logisim project 8-1 Mux.circ as structural Verilog: 5 circuits, main circuit 8-1 Mux (8)
module _8_1_Mux__16 (
  input  [15:0] _0,
  input  [15:0] _1,
  input  [15:0] _2,
  input  [15:0] _3,
  input  [15:0] _4,
  input  [15:0] _5,
  input  [15:0] _6,
  input  [15:0] _7,
  input  [2:0] in_9,
  output [15:0] out_10
);

  wire [15:0] n4_1_mux_16_1_y, n4_1_mux_16_2_y;

  _4_1_Mux__16 u_4_1_mux_16_1 (._0(_0), ._1(_1), ._2(_2), ._3(_3), .Select(in_9[1:0]), .Y(n4_1_mux_16_1_y));
  _4_1_Mux__16 u_4_1_mux_16_2 (._0(_4), ._1(_5), ._2(_6), ._3(_7), .Select(in_9[1:0]), .Y(n4_1_mux_16_2_y));
  _2_1_Mux__16 u_2_1_mux_16_1 (._0(n4_1_mux_16_1_y), ._1(n4_1_mux_16_2_y), .Select(in_9[2]), .Y(out_10));
endmodule

module _8_1_Mux__8 (
  input  [7:0] _0,
  input  [7:0] _1,
  input  [7:0] _2,
  input  [7:0] _3,
  input  [7:0] _4,
  input  [7:0] _5,
  input  [7:0] _6,
  input  [7:0] _7,
  input  [2:0] in_9,
  output [7:0] out_10
);

  wire [7:0] n4_1_mux_8_1_y, n4_1_mux_8_2_y;

  _4_1_Mux__8 u_4_1_mux_8_1 (._3(_3), ._2(_2), ._1(_1), ._0(_0), .Select(in_9[1:0]), .Y(n4_1_mux_8_1_y));
  _4_1_Mux__8 u_4_1_mux_8_2 (._3(_7), ._2(_6), ._1(_5), ._0(_4), .Select(in_9[1:0]), .Y(n4_1_mux_8_2_y));
  _2_1_Mux__8 u_2_1_mux_8_1 (._1(n4_1_mux_8_2_y), ._0(n4_1_mux_8_1_y), .Select(in_9[2]), .Y(out_10));
endmodule

module _8_1_Mux__4 (
  input  [3:0] _0,
  input  [3:0] _1,
  input  [3:0] _2,
  input  [3:0] _3,
  input  [3:0] _4,
  input  [3:0] _5,
  input  [3:0] _6,
  input  [3:0] _7,
  input  [2:0] in_9,
  output [3:0] out_10
);

  wire [3:0] n4_1_mux_4_1_y, n4_1_mux_4_2_y;

  _4_1_Mux__4 u_4_1_mux_4_1 (._0(_0), ._1(_1), ._2(_2), ._3(_3), .Select(in_9[1:0]), .Y(n4_1_mux_4_1_y));
  _4_1_Mux__4 u_4_1_mux_4_2 (._0(_4), ._1(_5), ._2(_6), ._3(_7), .Select(in_9[1:0]), .Y(n4_1_mux_4_2_y));
  _2_1_Mux__4 u_2_1_mux_4_1 (._0(n4_1_mux_4_1_y), ._1(n4_1_mux_4_2_y), .Select(in_9[2]), .Y(out_10));
endmodule

module _8_1_Mux__2 (
  input  [1:0] _0,
  input  [1:0] _1,
  input  [1:0] _2,
  input  [1:0] _3,
  input  [1:0] _4,
  input  [1:0] _5,
  input  [1:0] _6,
  input  [1:0] _7,
  input  [2:0] in_9,
  output [1:0] out_10
);

  wire [1:0] n4_1_mux_2_1_y, n4_1_mux_2_2_y;

  _4_1_Mux__2 u_4_1_mux_2_1 (._0(_0), ._1(_1), ._2(_2), ._3(_3), .Select(in_9[1:0]), .Y(n4_1_mux_2_1_y));
  _4_1_Mux__2 u_4_1_mux_2_2 (._0(_4), ._1(_5), ._2(_6), ._3(_7), .Select(in_9[1:0]), .Y(n4_1_mux_2_2_y));
  _2_1_Mux__2 u_2_1_mux_2_1 (._0(n4_1_mux_2_1_y), ._1(n4_1_mux_2_2_y), .Select(in_9[2]), .Y(out_10));
endmodule

module _8_1_Mux__1 (
  input  _0,
  input  _1,
  input  _2,
  input  _3,
  input  _4,
  input  _5,
  input  _6,
  input  _7,
  input  [2:0] in_9,
  output out_10
);

  wire n4_1_mux_1_1_y, n4_1_mux_1_2_y;

  _4_1_Mux__1 u_4_1_mux_1_1 (._0(_0), ._1(_1), ._2(_2), ._3(_3), .Select(in_9[1:0]), .Y(n4_1_mux_1_1_y));
  _4_1_Mux__1 u_4_1_mux_1_2 (._0(_4), ._1(_5), ._2(_6), ._3(_7), .Select(in_9[1:0]), .Y(n4_1_mux_1_2_y));
  _2_1_Mux__1 u_2_1_mux_1_1 (._0(n4_1_mux_1_1_y), ._1(n4_1_mux_1_2_y), .Select(in_9[2]), .Y(out_10));
endmodule
