// Logisim project Mux Test.circ as structural Verilog: 1 circuit, main circuit main
module main (
  input  [3:0] in_1
);

  wire _1_out;
  wire [1:0] n2_1_demux_2_1__0, n2_1_demux_2_1__1;
  wire [15:0] n16_1_mux_16_1_out_18;

  _2_1_Demux__2 u_2_1_demux_2_1 (._0(n2_1_demux_2_1__0), ._1(n2_1_demux_2_1__1), .Y(2'b10), .Select(_1_out));
  // Probe on n2_1_demux_2_1__0
  // Probe on n2_1_demux_2_1__1
  Button _1 (.out(_1_out));
  _16_1_Mux__16 u_16_1_mux_16_1 (
    ._0({16{1'b0}}), ._1(16'h1), ._2(16'h2), ._3(16'h3), ._4(16'h4), ._5(16'h5), ._6(16'h6), ._7(16'h7),
    .in_17(in_1), ._8(16'h8), .out_18(n16_1_mux_16_1_out_18), ._9(16'h9), ._10(16'ha), ._11(16'hb),
    ._12(16'hc), ._13(16'hd), ._14(16'he), ._15(16'hf));
  // Probe on n16_1_mux_16_1_out_18
endmodule
