// Logisim project D Flip Flop.circ as structural Verilog: 1 circuit, main circuit D_Flip_Flop_5c92dceb
module D_Flip_Flop_5c92dceb (
  input  Clr,
  input  Clock,
  input  En,
  input  Data,
  output Output
);

  wire and_1_out, and_2_out, and_3_out, error_detector_1_dbfb092c_1_out, nor_2_out, not_1_out, or_1_out,
       pulse_detect_78353950_1_pulse;

  Pulse_Detect_78353950 pulse_detect_78353950_1 (.Clock(Clock), .Pulse(pulse_detect_78353950_1_pulse));
  and and_1 (and_1_out, pulse_detect_78353950_1_pulse, En);
  not not_1 (not_1_out, Data);
  and and_2 (and_2_out, and_1_out, not_1_out);
  and and_3 (and_3_out, and_1_out, Data);
  nor nor_1 (Output, and_2_out, Clr, or_1_out);
  or or_1 (or_1_out, nor_2_out, error_detector_1_dbfb092c_1_out);
  nor nor_2 (nor_2_out, Output, and_3_out);
  Error_Detector_1_dbfb092c error_detector_1_dbfb092c_1 (.In(nor_2_out), .Out(error_detector_1_dbfb092c_1_out));

  // Notes on the sheet:
  //   Data: pull=down
  //   En: pull=up
endmodule
