// Logisim project JK Flip Flop.circ as structural Verilog: 1 circuit, main circuit JK_Flip_Flop_0cb27562
module JK_Flip_Flop_0cb27562 (
  input  Clock,
  input  K,
  input  En,
  input  J,
  input  Clear,
  output Output
);

  wire and_1_out, and_2_out, and_3_out, and_4_out, error_detector_1_dbfb092c_1_out,
       error_to_high_1_d72b71e8_1_out, error_to_high_1_d72b71e8_2_out, nor_1_out,
       pulse_detect_78353950_1_pulse;

  Pulse_Detect_78353950 pulse_detect_78353950_1 (.Clock(Clock), .Pulse(pulse_detect_78353950_1_pulse));
  Error_to_high_1_d72b71e8 error_to_high_1_d72b71e8_1 (.In(nor_1_out), .Out(error_to_high_1_d72b71e8_1_out));
  and and_1 (and_1_out, pulse_detect_78353950_1_pulse, En);
  Error_to_high_1_d72b71e8 error_to_high_1_d72b71e8_2 (.In(Output), .Out(error_to_high_1_d72b71e8_2_out));
  and and_2 (and_2_out, error_to_high_1_d72b71e8_1_out, K, and_1_out);
  and and_3 (and_3_out, and_1_out, J, error_to_high_1_d72b71e8_2_out);
  nor nor_1 (nor_1_out, and_2_out, and_4_out);
  and and_4 (and_4_out, Output, ~Clear, ~error_detector_1_dbfb092c_1_out);  // AND_Gate
  nor nor_2 (Output, nor_1_out, and_3_out);
  Error_Detector_1_dbfb092c error_detector_1_dbfb092c_1 (.In(Output), .Out(error_detector_1_dbfb092c_1_out));

  // Notes on the sheet:
  //   J: pull=down
  //   K: pull=down
  //   En: pull=up
endmodule
