// Logisim project D Latch.circ as structural Verilog: 1 circuit, main circuit D_Latch_3f9c06d7
module D_Latch_3f9c06d7 (
  input  En,
  input  Clear,
  input  Data,
  output Output
);

  wire and_1_out, and_2_out, error_to_low_1_b2f6d6ef_1_out, nor_2_out, not_1_out;

  and and_1 (and_1_out, En, not_1_out);
  not not_1 (not_1_out, Data);
  and and_2 (and_2_out, En, Data);
  nor nor_1 (Output, and_1_out, Clear, nor_2_out);
  Error_to_low_1_b2f6d6ef error_to_low_1_b2f6d6ef_1 (.In(Output), .Out(error_to_low_1_b2f6d6ef_1_out));
  nor nor_2 (nor_2_out, error_to_low_1_b2f6d6ef_1_out, and_2_out);

  // Notes on the sheet:
  //   Data: pull=down
  //   En: pull=up
  //   Clear: pull=down
endmodule
