// Logisim project SR Latch.circ as structural Verilog: 1 circuit, main circuit SR_Latch_c674d661
module SR_Latch_c674d661 (
  input  Reset,
  input  Set,
  output Output
);

  wire error_to_low_1_b2f6d6ef_1_out, nor_2_out;

  nor nor_1 (Output, Reset, nor_2_out);
  Error_to_low_1_b2f6d6ef error_to_low_1_b2f6d6ef_1 (.In(Output), .Out(error_to_low_1_b2f6d6ef_1_out));
  nor nor_2 (nor_2_out, error_to_low_1_b2f6d6ef_1_out, Set);

  // Notes on the sheet:
  //   Set: pull=down
  //   Reset: pull=down
endmodule
