// Logisim project Latch Register.circ as structural Verilog: 5 circuits, main circuit Latch_Register_1_b56ba028
module Latch_Register_1_b56ba028 (
  input  Clear,
  input  In,
  input  W,
  output Out
);

  wire and_1_out, not_1_out, z_detector_1_be9a67f0_1_out_2;

  D_Latch_3f9c06d7 d_latch_3f9c06d7_1 (.Data(In), .En(and_1_out), .Clear(Clear), .Output(Out));
  and and_1 (and_1_out, not_1_out, W);
  Z_Detector_1_be9a67f0 z_detector_1_be9a67f0_1 (.in_1(In), .out_2(z_detector_1_be9a67f0_1_out_2));
  not not_1 (not_1_out, z_detector_1_be9a67f0_1_out_2);
endmodule

module Latch_Register_2_da73ad48 (
  input  [1:0] In,
  input  Clear,
  input  W,
  output [1:0] Out
);

  wire and_1_out, not_1_out, z_detector_1_be9a67f0_1_out_2;

  D_Latch_3f9c06d7 d_latch_3f9c06d7_1 (.Data(In[0]), .En(and_1_out), .Clear(Clear), .Output(Out[0]));
  D_Latch_3f9c06d7 d_latch_3f9c06d7_2 (.Data(In[1]), .En(and_1_out), .Clear(Clear), .Output(Out[1]));
  Z_Detector_1_be9a67f0 z_detector_1_be9a67f0_1 (.in_1(In[1]), .out_2(z_detector_1_be9a67f0_1_out_2));
  not not_1 (not_1_out, z_detector_1_be9a67f0_1_out_2);
  and and_1 (and_1_out, not_1_out, W);
endmodule

module Latch_Register_4_cab8ea02 (
  input  [3:0] In,
  input  Clear,
  input  W,
  output [3:0] Out
);

  wire and_1_out, not_1_out, z_detector_1_be9a67f0_1_out_2;

  D_Latch_3f9c06d7 d_latch_3f9c06d7_1 (.Data(In[0]), .En(and_1_out), .Clear(Clear), .Output(Out[0]));
  D_Latch_3f9c06d7 d_latch_3f9c06d7_2 (.Data(In[1]), .En(and_1_out), .Clear(Clear), .Output(Out[1]));
  D_Latch_3f9c06d7 d_latch_3f9c06d7_3 (.Data(In[2]), .En(and_1_out), .Clear(Clear), .Output(Out[2]));
  D_Latch_3f9c06d7 d_latch_3f9c06d7_4 (.Data(In[3]), .En(and_1_out), .Clear(Clear), .Output(Out[3]));
  Z_Detector_1_be9a67f0 z_detector_1_be9a67f0_1 (.in_1(In[3]), .out_2(z_detector_1_be9a67f0_1_out_2));
  not not_1 (not_1_out, z_detector_1_be9a67f0_1_out_2);
  and and_1 (and_1_out, not_1_out, W);
endmodule

module Latch_Register_8_dfa3016f (
  input  [7:0] In,
  input  Clear,
  input  W,
  output [7:0] Out
);

  wire d_latch_3f9c06d7_7_p2, not_1_out, z_detector_1_be9a67f0_1_out_2;

  Z_Detector_1_be9a67f0 z_detector_1_be9a67f0_1 (.in_1(In[7]), .out_2(z_detector_1_be9a67f0_1_out_2));
  not not_1 (not_1_out, z_detector_1_be9a67f0_1_out_2);
  D_Latch_3f9c06d7 d_latch_3f9c06d7_1 (.Data(In[0]), .En(d_latch_3f9c06d7_7_p2), .Clear(Clear), .Output(Out[0]));
  D_Latch_3f9c06d7 d_latch_3f9c06d7_2 (.Data(In[1]), .En(d_latch_3f9c06d7_7_p2), .Clear(Clear), .Output(Out[1]));
  D_Latch_3f9c06d7 d_latch_3f9c06d7_3 (.Data(In[2]), .En(d_latch_3f9c06d7_7_p2), .Clear(Clear), .Output(Out[2]));
  D_Latch_3f9c06d7 d_latch_3f9c06d7_4 (.Data(In[3]), .En(d_latch_3f9c06d7_7_p2), .Clear(Clear), .Output(Out[3]));
  D_Latch_3f9c06d7 d_latch_3f9c06d7_5 (.Data(In[4]), .En(d_latch_3f9c06d7_7_p2), .Clear(Clear), .Output(Out[4]));
  D_Latch_3f9c06d7 d_latch_3f9c06d7_6 (.Data(In[5]), .En(d_latch_3f9c06d7_7_p2), .Clear(Clear), .Output(Out[5]));
  // D_Latch_3f9c06d7 d_latch_3f9c06d7_7: pin names not known; wires that end beside it: In[6], d_latch_3f9c06d7_7_p2, Clear, Out[6]
  D_Latch_3f9c06d7 d_latch_3f9c06d7_8 (.Data(In[7]), .En(d_latch_3f9c06d7_7_p2), .Clear(Clear), .Output(Out[7]));
  and and_1 (d_latch_3f9c06d7_7_p2, not_1_out, W);

  // Notes on the sheet:
  //   If bit 7 has high impedance, then enable is explicitly disabled
endmodule

module Latch_Register_16_3493f870 (
  input  Clear,
  input  [15:0] In,
  input  W,
  output [15:0] Out
);

  wire and_1_out, Write, Z_1_10cb6efc, Z_2_81575f89, z_detector_1_be9a67f0_1_out_2,
       z_detector_1_be9a67f0_2_out_2;

  Z_Detector_1_be9a67f0 z_detector_1_be9a67f0_1 (.in_1(In[15]), .out_2(z_detector_1_be9a67f0_1_out_2));
  not not_1 (Z_2_81575f89, z_detector_1_be9a67f0_1_out_2);
  and and_1 (and_1_out, Z_1_10cb6efc, Z_2_81575f89);
  D_Latch_3f9c06d7 d_latch_3f9c06d7_1 (.Data(In[8]), .En(Write), .Clear(Clear), .Output(Out[8]));
  D_Latch_3f9c06d7 d_latch_3f9c06d7_2 (.Data(In[9]), .En(Write), .Clear(Clear), .Output(Out[9]));
  D_Latch_3f9c06d7 d_latch_3f9c06d7_3 (.Data(In[10]), .En(Write), .Clear(Clear), .Output(Out[10]));
  D_Latch_3f9c06d7 d_latch_3f9c06d7_4 (.Data(In[11]), .En(Write), .Clear(Clear), .Output(Out[11]));
  D_Latch_3f9c06d7 d_latch_3f9c06d7_5 (.Data(In[12]), .En(Write), .Clear(Clear), .Output(Out[12]));
  D_Latch_3f9c06d7 d_latch_3f9c06d7_6 (.Data(In[13]), .En(Write), .Clear(Clear), .Output(Out[13]));
  D_Latch_3f9c06d7 d_latch_3f9c06d7_7 (.Data(In[14]), .En(Write), .Clear(Clear), .Output(Out[14]));
  D_Latch_3f9c06d7 d_latch_3f9c06d7_8 (.Data(In[15]), .En(Write), .Clear(Clear), .Output(Out[15]));
  and and_2 (Write, and_1_out, W);
  Z_Detector_1_be9a67f0 z_detector_1_be9a67f0_2 (.in_1(In[7]), .out_2(z_detector_1_be9a67f0_2_out_2));
  not not_2 (Z_1_10cb6efc, z_detector_1_be9a67f0_2_out_2);
  D_Latch_3f9c06d7 d_latch_3f9c06d7_9 (.Data(In[0]), .En(Write), .Clear(Clear), .Output(Out[0]));
  D_Latch_3f9c06d7 d_latch_3f9c06d7_10 (.Data(In[1]), .En(Write), .Clear(Clear), .Output(Out[1]));
  D_Latch_3f9c06d7 d_latch_3f9c06d7_11 (.Data(In[2]), .En(Write), .Clear(Clear), .Output(Out[2]));
  D_Latch_3f9c06d7 d_latch_3f9c06d7_12 (.Data(In[3]), .En(Write), .Clear(Clear), .Output(Out[3]));
  D_Latch_3f9c06d7 d_latch_3f9c06d7_13 (.Data(In[4]), .En(Write), .Clear(Clear), .Output(Out[4]));
  D_Latch_3f9c06d7 d_latch_3f9c06d7_14 (.Data(In[5]), .En(Write), .Clear(Clear), .Output(Out[5]));
  D_Latch_3f9c06d7 d_latch_3f9c06d7_15 (.Data(In[6]), .En(Write), .Clear(Clear), .Output(Out[6]));
  D_Latch_3f9c06d7 d_latch_3f9c06d7_16 (.Data(In[7]), .En(Write), .Clear(Clear), .Output(Out[7]));

  // Other names for the same wires on the sheet: Clr = Clear; In_1_bf356adb[7:0] = In[7:0];
  //   In_2_4429d811[7:0] = In[15:8]; Out_1_2ab55e17[7:0] = Out[7:0]; Out_2_039e4930[7:0] = Out[15:8]

  // Notes on the sheet:
  //   If bit 7 or 15 have high impedance, then enable is explicitly disabled
endmodule
