// Logisim project Register.circ as structural Verilog: 5 circuits, main circuit Register_1_d11bd6e6
module Register_1_d11bd6e6 (
  input  Clk,
  input  Clear,
  input  In,
  input  W,
  output Out
);

  wire and_1_out, not_1_out, z_detector_1_be9a67f0_1_out_2;

  D_Flip_Flop_5c92dceb d_flip_flop_5c92dceb_1 (.Clr(Clear), .Data(In), .Clock(Clk), .En(and_1_out), .Output(Out));
  and and_1 (and_1_out, not_1_out, W);
  Z_Detector_1_be9a67f0 z_detector_1_be9a67f0_1 (.in_1(In), .out_2(z_detector_1_be9a67f0_1_out_2));
  not not_1 (not_1_out, z_detector_1_be9a67f0_1_out_2);

  // Notes on the sheet:
  //   Clear: pull=down
endmodule

module Register_2_0f5e3507 (
  input  Clk,
  input  [1:0] In,
  input  Clear,
  input  W,
  output [1:0] Out
);

  wire and_1_out, not_1_out, z_detector_1_be9a67f0_1_out_2;

  D_Flip_Flop_5c92dceb d_flip_flop_5c92dceb_1 (.Clr(Clear), .Data(In[0]), .Clock(Clk), .En(and_1_out), .Output(Out[0]));
  D_Flip_Flop_5c92dceb d_flip_flop_5c92dceb_2 (.Clr(Clear), .Data(In[1]), .Clock(Clk), .En(and_1_out), .Output(Out[1]));
  Z_Detector_1_be9a67f0 z_detector_1_be9a67f0_1 (.in_1(In[1]), .out_2(z_detector_1_be9a67f0_1_out_2));
  not not_1 (not_1_out, z_detector_1_be9a67f0_1_out_2);
  and and_1 (and_1_out, not_1_out, W);

  // Notes on the sheet:
  //   Clear: pull=down
endmodule

module Register_4_00c0e107 (
  input  Clk,
  input  [3:0] In,
  input  Clear,
  input  W,
  output [3:0] Out
);

  wire and_1_out, not_1_out, z_detector_1_be9a67f0_1_out_2;

  D_Flip_Flop_5c92dceb d_flip_flop_5c92dceb_1 (.Clr(Clear), .Data(In[0]), .Clock(Clk), .En(and_1_out), .Output(Out[0]));
  D_Flip_Flop_5c92dceb d_flip_flop_5c92dceb_2 (.Clr(Clear), .Data(In[1]), .Clock(Clk), .En(and_1_out), .Output(Out[1]));
  D_Flip_Flop_5c92dceb d_flip_flop_5c92dceb_3 (.Clr(Clear), .Data(In[2]), .Clock(Clk), .En(and_1_out), .Output(Out[2]));
  D_Flip_Flop_5c92dceb d_flip_flop_5c92dceb_4 (.Clr(Clear), .Data(In[3]), .Clock(Clk), .En(and_1_out), .Output(Out[3]));
  Z_Detector_1_be9a67f0 z_detector_1_be9a67f0_1 (.in_1(In[3]), .out_2(z_detector_1_be9a67f0_1_out_2));
  not not_1 (not_1_out, z_detector_1_be9a67f0_1_out_2);
  and and_1 (and_1_out, not_1_out, W);

  // Notes on the sheet:
  //   Clear: pull=down
endmodule

module Register_8_252a90b2 (
  input  Clk,
  input  [7:0] In,
  input  Clear,
  input  W,
  output [7:0] Out
);

  wire and_1_out, not_1_out, z_detector_1_be9a67f0_1_out_2;

  Z_Detector_1_be9a67f0 z_detector_1_be9a67f0_1 (.in_1(In[7]), .out_2(z_detector_1_be9a67f0_1_out_2));
  not not_1 (not_1_out, z_detector_1_be9a67f0_1_out_2);
  D_Flip_Flop_5c92dceb d_flip_flop_5c92dceb_1 (.Clr(Clear), .Data(In[0]), .Clock(Clk), .En(and_1_out), .Output(Out[0]));
  D_Flip_Flop_5c92dceb d_flip_flop_5c92dceb_2 (.Clr(Clear), .Data(In[1]), .Clock(Clk), .En(and_1_out), .Output(Out[1]));
  D_Flip_Flop_5c92dceb d_flip_flop_5c92dceb_3 (.Clr(Clear), .Data(In[2]), .Clock(Clk), .En(and_1_out), .Output(Out[2]));
  D_Flip_Flop_5c92dceb d_flip_flop_5c92dceb_4 (.Clr(Clear), .Data(In[3]), .Clock(Clk), .En(and_1_out), .Output(Out[3]));
  D_Flip_Flop_5c92dceb d_flip_flop_5c92dceb_5 (.Clr(Clear), .Data(In[4]), .Clock(Clk), .En(and_1_out), .Output(Out[4]));
  D_Flip_Flop_5c92dceb d_flip_flop_5c92dceb_6 (.Clr(Clear), .Data(In[5]), .Clock(Clk), .En(and_1_out), .Output(Out[5]));
  D_Flip_Flop_5c92dceb d_flip_flop_5c92dceb_7 (.Clr(Clear), .Data(In[6]), .Clock(Clk), .En(and_1_out), .Output(Out[6]));
  D_Flip_Flop_5c92dceb d_flip_flop_5c92dceb_8 (.Clr(Clear), .Data(In[7]), .Clock(Clk), .En(and_1_out), .Output(Out[7]));
  and and_1 (and_1_out, not_1_out, W);

  // Notes on the sheet:
  //   Clear: pull=down
  //   If bit 7 has high impedance, then enable is explicitly disabled
endmodule

module Register_16_2fb72861 (
  input  Clk,
  input  Clear,
  input  [15:0] In,
  input  W,
  output [15:0] Out
);

  wire and_1_out, Write, Z_1_b302741d, Z_2_d3dc9dec, z_detector_1_be9a67f0_1_out_2,
       z_detector_1_be9a67f0_2_out_2;

  Z_Detector_1_be9a67f0 z_detector_1_be9a67f0_1 (.in_1(In[15]), .out_2(z_detector_1_be9a67f0_1_out_2));
  not not_1 (Z_2_d3dc9dec, z_detector_1_be9a67f0_1_out_2);
  and and_1 (and_1_out, Z_1_b302741d, Z_2_d3dc9dec);
  D_Flip_Flop_5c92dceb d_flip_flop_5c92dceb_1 (.Clr(Clear), .Data(In[8]), .Clock(Clk), .En(Write), .Output(Out[8]));
  D_Flip_Flop_5c92dceb d_flip_flop_5c92dceb_2 (.Clr(Clear), .Data(In[9]), .Clock(Clk), .En(Write), .Output(Out[9]));
  D_Flip_Flop_5c92dceb d_flip_flop_5c92dceb_3 (.Clr(Clear), .Data(In[10]), .Clock(Clk), .En(Write), .Output(Out[10]));
  D_Flip_Flop_5c92dceb d_flip_flop_5c92dceb_4 (.Clr(Clear), .Data(In[11]), .Clock(Clk), .En(Write), .Output(Out[11]));
  D_Flip_Flop_5c92dceb d_flip_flop_5c92dceb_5 (.Clr(Clear), .Data(In[12]), .Clock(Clk), .En(Write), .Output(Out[12]));
  D_Flip_Flop_5c92dceb d_flip_flop_5c92dceb_6 (.Clr(Clear), .Data(In[13]), .Clock(Clk), .En(Write), .Output(Out[13]));
  D_Flip_Flop_5c92dceb d_flip_flop_5c92dceb_7 (.Clr(Clear), .Data(In[14]), .Clock(Clk), .En(Write), .Output(Out[14]));
  D_Flip_Flop_5c92dceb d_flip_flop_5c92dceb_8 (.Clr(Clear), .Data(In[15]), .Clock(Clk), .En(Write), .Output(Out[15]));
  and and_2 (Write, and_1_out, W);
  Z_Detector_1_be9a67f0 z_detector_1_be9a67f0_2 (.in_1(In[7]), .out_2(z_detector_1_be9a67f0_2_out_2));
  not not_2 (Z_1_b302741d, z_detector_1_be9a67f0_2_out_2);
  D_Flip_Flop_5c92dceb d_flip_flop_5c92dceb_9 (.Clr(Clear), .Data(In[0]), .Clock(Clk), .En(Write), .Output(Out[0]));
  D_Flip_Flop_5c92dceb d_flip_flop_5c92dceb_10 (.Clr(Clear), .Data(In[1]), .Clock(Clk), .En(Write), .Output(Out[1]));
  D_Flip_Flop_5c92dceb d_flip_flop_5c92dceb_11 (.Clr(Clear), .Data(In[2]), .Clock(Clk), .En(Write), .Output(Out[2]));
  D_Flip_Flop_5c92dceb d_flip_flop_5c92dceb_12 (.Clr(Clear), .Data(In[3]), .Clock(Clk), .En(Write), .Output(Out[3]));
  D_Flip_Flop_5c92dceb d_flip_flop_5c92dceb_13 (.Clr(Clear), .Data(In[4]), .Clock(Clk), .En(Write), .Output(Out[4]));
  D_Flip_Flop_5c92dceb d_flip_flop_5c92dceb_14 (.Clr(Clear), .Data(In[5]), .Clock(Clk), .En(Write), .Output(Out[5]));
  D_Flip_Flop_5c92dceb d_flip_flop_5c92dceb_15 (.Clr(Clear), .Data(In[6]), .Clock(Clk), .En(Write), .Output(Out[6]));
  D_Flip_Flop_5c92dceb d_flip_flop_5c92dceb_16 (.Clr(Clear), .Data(In[7]), .Clock(Clk), .En(Write), .Output(Out[7]));

  // Other names for the same wires on the sheet: Clr = Clear; In_1_9ba56319[7:0] = In[7:0];
  //   In_2_71de0458[7:0] = In[15:8]; Out_1_3c4298ac[7:0] = Out[7:0]; Out_2_5f590edc[7:0] = Out[15:8]

  // Notes on the sheet:
  //   Clear: pull=down
  //   If bit 7 or 15 have high impedance, then enable is explicitly disabled
endmodule
