// Logisim project Priority Encoder.circ as structural Verilog: 5 circuits, main circuit L_2_1_Priority_Encoder_76bde91d
module L_2_1_Priority_Encoder_76bde91d (
  input  [1:0] In,
  output V,
  output Out
);

  or or_1 (V, In[0], In[1]);

  assign Out = In[1];
endmodule

module L_4_2_Priority_Encoder_5bb722dd (
  input  [3:0] In,
  output V,
  output [1:0] Out
);

  wire and_1_out;

  or or_1 (V, In[0], In[2], In[3], In[1]);
  or or_2 (Out[1], In[2], In[3]);
  and and_1 (and_1_out, In[1], ~In[2]);  // AND_Gate
  or or_3 (Out[0], and_1_out, In[3]);
endmodule

module L_8_3_Priority_Encoder_8cb8f1ab (
  input  [7:0] In,
  output V,
  output [2:0] Out
);

  wire and_1_out, and_2_out, and_3_out, and_4_out, and_5_out;

  or or_1 (V, In[6], In[1], In[4], In[5], In[7], In[2], In[3], In[0]);
  and and_1 (and_1_out, ~In[6], ~In[4], ~In[2], In[1]);  // AND_Gate
  and and_2 (and_2_out, ~In[4], ~In[6], In[3]);  // AND_Gate
  and and_3 (and_3_out, ~In[6], In[5]);  // AND_Gate
  and and_4 (and_4_out, ~In[4], ~In[5], In[3]);  // AND_Gate
  and and_5 (and_5_out, ~In[5], ~In[4], In[2]);  // AND_Gate
  or or_2 (Out[0], In[7], and_1_out, and_2_out, and_3_out);
  or or_3 (Out[1], and_4_out, and_5_out, In[6], In[7]);
  or or_4 (Out[2], In[4], In[5], In[6], In[7]);
endmodule

module L_16_4_Priority_Encoder_e648d634 (
  input  [15:0] in_1,
  output [3:0] Out,
  output V
);

  wire [1:0] l_4_2_priority_encoder_5bb722dd_1_out, l_4_2_priority_encoder_5bb722dd_2_out,
       l_4_2_priority_encoder_5bb722dd_3_out, l_4_2_priority_encoder_5bb722dd_4_out;
  wire [3:0] l_4_2_priority_encoder_5bb722dd_1_v;

  L_4_2_Priority_Encoder_5bb722dd l_4_2_priority_encoder_5bb722dd_1 (
    .In(in_1[3:0]), .V(l_4_2_priority_encoder_5bb722dd_1_v[0]), .Out(l_4_2_priority_encoder_5bb722dd_1_out));
  L_4_2_Priority_Encoder_5bb722dd l_4_2_priority_encoder_5bb722dd_2 (
    .In(in_1[7:4]), .V(l_4_2_priority_encoder_5bb722dd_1_v[1]), .Out(l_4_2_priority_encoder_5bb722dd_2_out));
  L_4_2_Priority_Encoder_5bb722dd l_4_2_priority_encoder_5bb722dd_3 (
    .In(in_1[11:8]), .V(l_4_2_priority_encoder_5bb722dd_1_v[2]), .Out(l_4_2_priority_encoder_5bb722dd_3_out));
  L_4_2_Priority_Encoder_5bb722dd l_4_2_priority_encoder_5bb722dd_4 (
    .In(in_1[15:12]), .V(l_4_2_priority_encoder_5bb722dd_1_v[3]), .Out(l_4_2_priority_encoder_5bb722dd_4_out));
  Mux_2 mux_2_1 (
    .p2(l_4_2_priority_encoder_5bb722dd_3_out), .p3(l_4_2_priority_encoder_5bb722dd_4_out),
    .Select(Out[3:2]), .p0(l_4_2_priority_encoder_5bb722dd_1_out),
    .p1(l_4_2_priority_encoder_5bb722dd_2_out), .Y(Out[1:0]));
  L_4_2_Priority_Encoder_5bb722dd l_4_2_priority_encoder_5bb722dd_5 (
    .In(l_4_2_priority_encoder_5bb722dd_1_v), .V(V), .Out(Out[3:2]));
endmodule

module L_32_5_Priority_Encoder_c1276c5e (
  input  [31:0] in_1,
  output [4:0] Out,
  output V
);

  wire [1:0] l_16_4_priority_encoder_e648d634_1_v;
  wire [3:0] l_16_4_priority_encoder_e648d634_1_out, l_16_4_priority_encoder_e648d634_2_out;

  L_16_4_Priority_Encoder_e648d634 l_16_4_priority_encoder_e648d634_1 (
    .in_1(in_1[15:0]), .Out(l_16_4_priority_encoder_e648d634_1_out),
    .V(l_16_4_priority_encoder_e648d634_1_v[0]));
  L_16_4_Priority_Encoder_e648d634 l_16_4_priority_encoder_e648d634_2 (
    .in_1(in_1[31:16]), .Out(l_16_4_priority_encoder_e648d634_2_out),
    .V(l_16_4_priority_encoder_e648d634_1_v[1]));
  Mux_4 mux_4_1 (
    .p0(l_16_4_priority_encoder_e648d634_1_out), .p1(l_16_4_priority_encoder_e648d634_2_out),
    .Select(Out[4]), .Y(Out[3:0]));
  L_2_1_Priority_Encoder_76bde91d l_2_1_priority_encoder_76bde91d_1 (
    .In(l_16_4_priority_encoder_e648d634_1_v), .Out(Out[4]), .V(V));
endmodule
