// Logisim project Right.circ as structural Verilog: 1 circuit, main circuit Right_Shifter_531e43bc
module Right_Shifter_531e43bc (
  input  [7:0] in_1,
  output [7:0] out_2
);


  assign out_2 = {in_1[0], in_1[7:1]};
endmodule
